// Logisim project 16bitcomputer.circ as structural Verilog: 47 circuits, main circuit main
module main (
  input  CLOCK,
  input  [15:0] in_2,
  output [15:0] out_3,
  output [15:0] out_4,
  output [15:0] out_5,
  output [15:0] out_6,
  output [15:0] out_7,
  output [15:0] out_8
);

  wire and_1_out, and_2_out, CONTINUE_out, control_logic_unit_1_p9, control_logic_unit_1_p10,
       control_logic_unit_1_p14, control_logic_unit_1_p15, control_logic_unit_1_p16,
       control_logic_unit_1_p17, control_logic_unit_1_p18, RESET_out, undriven_2, xor_1_out;
  wire [3:0] control_logic_unit_1_p11, control_logic_unit_1_p12;
  wire [15:0] adder_1_out, multiplexer_1_out, sixteen_bit_program_counter_1_count,
       sixteen_bit_program_counter_2_count, sixteen_sixteen_register_1_base_pointer,
       sixteen_sixteen_register_1_output_a, sixteen_sixteen_register_1_output_b, undriven, X_AXIS_q, Y_AXIS_q;

  Button CONTINUE (.out(CONTINUE_out));
  xor xor_1 (xor_1_out, CONTINUE_out, ~control_logic_unit_1_p17);  // XOR_Gate
  and and_1 (and_1_out, CLOCK, xor_1_out);
  and and_2 (and_2_out, RESET_out, ~and_1_out);  // AND_Gate
  Button RESET (.out(RESET_out));
  SIXTEEN_BIT_PROGRAM_COUNTER sixteen_bit_program_counter_1 (
    .CLOCK(and_1_out), .RESET(and_2_out), .INP(out_4), .WRITE(control_logic_unit_1_p18),
    .COUNT(sixteen_bit_program_counter_1_count));
  RAM #(.addrWidth(16), .dataWidth(16), .enables("line"), .misaligned("true"), .\type ("nonvolatile")) ram_1 (
    .addr(sixteen_bit_program_counter_1_count), .clk(and_1_out), .dout(out_3));  // open: we, din
  SIXTEEN_BIT_PROGRAM_COUNTER sixteen_bit_program_counter_2 (
    .CLOCK(and_1_out), .COUNT(sixteen_bit_program_counter_2_count));  // open: RESET, INP, WRITE
  SIXTEEN_SIXTEEN_REGISTER sixteen_sixteen_register_1 (
    .RESET(and_2_out), .WRITE_Address(control_logic_unit_1_p11), .INPUT_Data(out_4),
    .ENABLE(control_logic_unit_1_p9), .CLOCK(and_1_out), .TIME_INPUT(sixteen_bit_program_counter_2_count),
    .USER_INPUT(undriven), .INPUT_ADDRESS_A(control_logic_unit_1_p11),
    .INPUT_ADDRESS_B(control_logic_unit_1_p12), .BASE_POINTER(sixteen_sixteen_register_1_base_pointer),
    .OUTPUT_B(sixteen_sixteen_register_1_output_b), .OUTPUT_A(sixteen_sixteen_register_1_output_a));
  Multiplexer #(.width(16)) multiplexer_1 (.in0(out_3), .in1(out_5), .out(multiplexer_1_out), .sel(undriven_2));
  RAM #(.addrWidth(16), .clearpin("true"), .dataWidth(16), .enables("line")) RAM_16x16_bit_RAM (
    .addr(adder_1_out), .we(control_logic_unit_1_p10), .clk(control_logic_unit_1_p10), .din(out_4),
    .dout(out_7), .clr(and_2_out));
  Adder #(.width(16)) adder_1 (
    .a(sixteen_sixteen_register_1_base_pointer), .b(multiplexer_1_out), .out(adder_1_out));  // open: cin, cout
  // CONTROL_LOGIC_UNIT control_logic_unit_1: pin names not known; wires that end beside it: sixteen_bit_program_counter_1_count, out_3, and_1_out, sixteen_sixteen_register_1_output_a, sixteen_sixteen_register_1_output_b, out_7, and_2_out, out_4, control_logic_unit_1_p9, control_logic_unit_1_p10, control_logic_unit_1_p11, control_logic_unit_1_p12, out_5, control_logic_unit_1_p14, control_logic_unit_1_p15, control_logic_unit_1_p16, control_logic_unit_1_p17, control_logic_unit_1_p18
  Register #(.width(16)) X_AXIS (
    .D(out_4), .en(control_logic_unit_1_p15), .clk(control_logic_unit_1_p15), .Q(X_AXIS_q), .clr(and_2_out));
  Register #(.width(16)) Y_AXIS (
    .D(out_4), .en(control_logic_unit_1_p16), .clk(control_logic_unit_1_p16), .Q(Y_AXIS_q), .clr(and_2_out));
  // RGB_Video #(.cursor("No Cursor"), .height(64), .scale(4), .width(64)) rgb_video_1: pin names not known; wires that end beside it: and_2_out, control_logic_unit_1_p14, control_logic_unit_1_p14, X_AXIS_q[5:0], Y_AXIS_q[5:0], out_4

  assign out_6 = out_3;
  assign out_8 = out_4;
endmodule

module TWO_MUX (
  input  S0,
  input  F1,
  input  F0,
  output Y
);

  wire and_1_out, and_2_out, not_1_out;

  not not_1 (not_1_out, S0);
  and and_1 (and_1_out, S0, F1);
  and and_2 (and_2_out, not_1_out, F0);
  or or_1 (Y, and_1_out, and_2_out);
endmodule

module SIXTEEN_MUX (
  input  S0,
  input  S1,
  input  S2,
  input  S3,
  input  F15,
  input  F14,
  input  F13,
  input  F12,
  input  F11,
  input  F10,
  input  F9,
  input  F8,
  input  F7,
  input  F6,
  input  F5,
  input  F4,
  input  F3,
  input  F2,
  input  F1,
  input  F0,
  output Y
);

  wire four_mux_1_y, four_mux_2_y, four_mux_3_y, four_mux_4_y;

  FOUR_MUX four_mux_1 (.S0(S1), .S1(S0), .F3(F15), .F2(F14), .F1(F13), .F0(F12), .Y(four_mux_1_y));
  FOUR_MUX four_mux_2 (.S0(S1), .S1(S0), .F3(F11), .F2(F10), .F1(F9), .F0(F8), .Y(four_mux_2_y));
  FOUR_MUX four_mux_3 (.S0(S1), .S1(S0), .F3(F7), .F2(F6), .F1(F5), .F0(F4), .Y(four_mux_3_y));
  FOUR_MUX four_mux_4 (.S0(S1), .S1(S0), .F3(F3), .F2(F2), .F1(F1), .F0(F0), .Y(four_mux_4_y));
  FOUR_MUX four_mux_5 (
    .S0(S2), .S1(S3), .F3(four_mux_1_y), .F2(four_mux_2_y), .F1(four_mux_3_y), .F0(four_mux_4_y), .Y(Y));
endmodule

module TWO_DEMUX (
  input  G,
  input  S0,
  output F1,
  output F0
);

  wire not_1_out;

  not not_1 (not_1_out, S0);
  and and_1 (F1, G, not_1_out);
  and and_2 (F0, G, S0);
endmodule

module FOUR_MUX (
  input  S0,
  input  S1,
  input  F3,
  input  F2,
  input  F1,
  input  F0,
  output Y
);

  wire and_1_out, and_2_out, and_3_out, and_4_out, not_1_out, not_2_out;

  not not_1 (not_1_out, S0);
  not not_2 (not_2_out, S1);
  and and_1 (and_1_out, S0, S1, F3);
  and and_2 (and_2_out, S0, not_2_out, F2);
  and and_3 (and_3_out, S1, not_1_out, F1);
  and and_4 (and_4_out, not_2_out, not_1_out, F0);
  or or_1 (Y, and_1_out, and_2_out, and_3_out, and_4_out);
endmodule

module FOUR_DEMUX (
  input  G,
  input  S1,
  input  S0,
  output F3,
  output F2,
  output F1,
  output F0
);

  wire not_1_out, not_2_out;

  not not_1 (not_1_out, S1);
  not not_2 (not_2_out, S0);
  and and_1 (F3, G, S1, S0);
  and and_2 (F2, G, S1, not_2_out);
  and and_3 (F1, G, not_1_out, S0);
  and and_4 (F0, G, not_1_out, not_2_out);
endmodule

module SIXTEEN_DEMUX (
  input  G,
  input  S3,
  input  S2,
  input  S1,
  input  S0,
  output F15,
  output F14,
  output F13,
  output F12,
  output F11,
  output F10,
  output F9,
  output F8,
  output F7,
  output F6,
  output F5,
  output F4,
  output F3,
  output F2,
  output F1,
  output F0
);

  wire not_1_out, not_2_out, not_3_out, not_4_out;

  not not_1 (not_1_out, S3);
  not not_2 (not_2_out, S2);
  not not_3 (not_3_out, S1);
  not not_4 (not_4_out, S0);
  and and_1 (F15, G, S3, S2, S1, S0);
  and and_2 (F14, G, S3, S2, S1, not_4_out);
  and and_3 (F13, G, S3, S2, not_2_out, S0);
  and and_4 (F12, G, S3, S2, not_3_out, not_4_out);
  and and_5 (F11, G, S3, not_2_out, S1, S0);
  and and_6 (F10, G, S3, not_2_out, S1, not_4_out);
  and and_7 (F9, G, S3, not_2_out, not_3_out, S0);
  and and_8 (F8, G, S3, not_2_out, not_3_out, not_4_out);
  and and_9 (F7, G, not_1_out, S2, S1, S0);
  and and_10 (F6, G, not_1_out, S2, S1, not_4_out);
  and and_11 (F5, G, not_1_out, S2, not_3_out, S0);
  and and_12 (F4, G, not_1_out, S2, not_3_out, not_4_out);
  and and_13 (F3, G, not_1_out, not_2_out, S1, S0);
  and and_14 (F2, G, not_1_out, not_2_out, S1, not_4_out);
  and and_15 (F1, G, not_1_out, not_2_out, not_3_out, S0);
  and and_16 (F0, G, not_1_out, not_2_out, not_3_out, not_4_out);
endmodule

module FOUR_DECODER (
  input  S1,
  input  S0,
  output Y3,
  output Y2,
  output Y1,
  output Y0
);

  wire not_1_out, not_2_out;

  not not_1 (not_1_out, S1);
  not not_2 (not_2_out, S0);
  and and_1 (Y3, S1, S0);
  and and_2 (Y2, S1, not_2_out);
  and and_3 (Y1, not_1_out, S0);
  and and_4 (Y0, not_1_out, not_2_out);
endmodule

module EIGHT_DECODER (
  input  F2,
  input  F1,
  input  F0,
  output Y7,
  output Y6,
  output Y5,
  output Y4,
  output Y3,
  output Y2,
  output Y1,
  output Y0
);

  wire not_1_out, not_2_out, not_3_out;

  not not_1 (not_1_out, F2);
  not not_2 (not_2_out, F1);
  not not_3 (not_3_out, F0);
  and and_1 (Y7, F2, F1, F0);
  and and_2 (Y6, F2, F1, not_3_out);
  and and_3 (Y5, F2, not_2_out, F0);
  and and_4 (Y4, F2, not_2_out, not_3_out);
  and and_5 (Y3, not_1_out, F1, F0);
  and and_6 (Y2, not_1_out, F1, not_3_out);
  and and_7 (Y1, not_1_out, not_2_out, F0);
  and and_8 (Y0, not_3_out, not_2_out, not_1_out);
endmodule

module SIXTEEN_DECODER (
  input  F3,
  input  F2,
  input  F1,
  input  F0,
  output Y15,
  output Y14,
  output Y13,
  output Y12,
  output Y11,
  output Y10,
  output Y9,
  output Y8,
  output Y7,
  output Y6,
  output Y5,
  output Y4,
  output Y3,
  output Y2,
  output Y1,
  output Y0
);

  wire not_1_out, not_2_out, not_3_out, not_4_out;

  not not_1 (not_1_out, F3);
  not not_2 (not_2_out, F2);
  not not_3 (not_3_out, F1);
  not not_4 (not_4_out, F0);
  and and_1 (Y15, F3, F2, F1, F0);
  and and_2 (Y14, F3, F2, F1, not_4_out);
  and and_3 (Y13, F3, F2, not_3_out, F0);
  and and_4 (Y12, F3, F2, not_3_out, not_4_out);
  and and_5 (Y11, F3, not_2_out, F1, F0);
  and and_6 (Y10, F3, not_2_out, F1, not_4_out);
  and and_7 (Y9, F3, not_2_out, not_3_out, F0);
  and and_8 (Y8, F3, not_2_out, not_3_out, not_4_out);
  and and_9 (Y7, not_1_out, F2, F1, F0);
  and and_10 (Y6, not_1_out, F2, F1, not_4_out);
  and and_11 (Y5, not_1_out, F2, not_3_out, F0);
  and and_12 (Y4, not_1_out, F2, not_3_out, not_4_out);
  and and_13 (Y3, not_1_out, not_2_out, F1, F0);
  and and_14 (Y2, not_1_out, not_2_out, F1, not_4_out);
  and and_15 (Y1, not_1_out, not_2_out, not_3_out, F0);
  and and_16 (Y0, not_1_out, not_2_out, not_3_out, not_4_out);
endmodule

module D_LATCH (
  input  D,
  input  CLK,
  output Q,
  output NQ
);

  wire nand_1_out, nand_2_out, not_1_out;

  not not_1 (not_1_out, D);
  nand nand_1 (nand_1_out, D, CLK);
  nand nand_2 (nand_2_out, not_1_out, CLK);
  nand nand_3 (Q, nand_1_out, NQ);
  nand nand_4 (NQ, Q, nand_2_out);
endmodule

module T_LATCH (
  input  T,
  input  CLK,
  output Q,
  output NQ
);

  wire nand_1_out, nand_2_out;

  nand nand_1 (nand_1_out, NQ, T, CLK);
  nand nand_2 (nand_2_out, T, Q);
  nand nand_3 (Q, nand_1_out, NQ);
  nand nand_4 (NQ, Q, nand_2_out);
endmodule

module JK_LATCH (
  input  J,
  input  CLK,
  input  K,
  output Q,
  output NQ
);

  wire nand_1_out, nand_2_out;

  nand nand_1 (nand_1_out, NQ, J, CLK);
  nand nand_2 (nand_2_out, CLK, K, Q);
  nand nand_3 (Q, NQ, nand_1_out);
  nand nand_4 (NQ, nand_2_out, Q);
endmodule

module SR_LATCH (
  input  S,
  input  CLK,
  input  R,
  output Q,
  output NQ
);

  wire and_1_out, and_2_out;

  and and_1 (and_1_out, S, CLK);
  and and_2 (and_2_out, CLK, R);
  nor nor_1 (Q, NQ, and_1_out);
  nor nor_2 (NQ, and_2_out, Q);
endmodule

module EIGHT_BIT_REGISTER_RISING_EDGE (
  input  [7:0] DATA,
  input  WRITE,
  input  CLK,
  input  RESET,
  output [7:0] out_5
);

  wire and_1_out, and_2_out, and_3_out, and_4_out, and_5_out, and_6_out, and_7_out, and_8_out;

  D_Flip_Flop d_ff_1 (.D(and_1_out), .clk(CLK), .Q(out_5[0]), .reset(RESET));  // open: Qn, preset
  and and_1 (and_1_out, DATA[0], WRITE);
  D_Flip_Flop d_ff_2 (.D(and_2_out), .clk(CLK), .Q(out_5[1]), .reset(RESET));  // open: Qn, preset
  and and_2 (and_2_out, DATA[1], WRITE);
  D_Flip_Flop d_ff_3 (.D(and_3_out), .clk(CLK), .Q(out_5[2]), .reset(RESET));  // open: Qn, preset
  and and_3 (and_3_out, DATA[2], WRITE);
  D_Flip_Flop d_ff_4 (.D(and_4_out), .clk(CLK), .Q(out_5[3]), .reset(RESET));  // open: Qn, preset
  and and_4 (and_4_out, DATA[3], WRITE);
  D_Flip_Flop d_ff_5 (.D(and_5_out), .clk(CLK), .Q(out_5[4]), .reset(RESET));  // open: Qn, preset
  and and_5 (and_5_out, DATA[4], WRITE);
  D_Flip_Flop d_ff_6 (.D(and_6_out), .clk(CLK), .Q(out_5[5]), .reset(RESET));  // open: Qn, preset
  and and_6 (and_6_out, DATA[5], WRITE);
  D_Flip_Flop d_ff_7 (.D(and_7_out), .clk(CLK), .Q(out_5[6]), .reset(RESET));  // open: Qn, preset
  and and_7 (and_7_out, DATA[6], WRITE);
  D_Flip_Flop d_ff_8 (.D(and_8_out), .clk(CLK), .Q(out_5[7]), .reset(RESET));  // open: Qn, preset
  and and_8 (and_8_out, DATA[7], WRITE);
endmodule

module D_FLIP_FLOP_RISING_EDGE (
  input  PRESET,
  input  D,
  input  CLK,
  input  RESET,
  output Q,
  output NQ
);

  wire nand_1_out, nand_2_out, nand_3_out, nand_4_out, nand_5_out, nand_6_out, not_1_out, not_2_out;

  not not_1 (not_1_out, D);
  nand nand_1 (nand_1_out, D, CLK);
  nand nand_2 (nand_2_out, not_1_out, CLK);
  nand nand_3 (nand_3_out, PRESET, nand_1_out, nand_4_out);
  nand nand_4 (nand_4_out, nand_3_out, nand_2_out, RESET);
  not not_2 (not_2_out, CLK);
  nand nand_5 (nand_5_out, nand_3_out, not_2_out);
  nand nand_6 (nand_6_out, nand_4_out, not_2_out);
  nand nand_7 (Q, PRESET, nand_5_out, NQ);
  nand nand_8 (NQ, Q, nand_6_out, RESET);
endmodule

module FULL_ADDER (
  input  A,
  input  B,
  input  CIN,
  output SUM,
  output COUT
);

  wire and_1_out, and_2_out, xor_1_out;

  xor xor_1 (xor_1_out, A, B);
  xor xor_2 (SUM, xor_1_out, CIN);
  and and_1 (and_1_out, CIN, xor_1_out);
  and and_2 (and_2_out, B, A);
  or or_1 (COUT, and_1_out, and_2_out);
endmodule

module HALF_ADDER (
  input  A,
  input  SUM,
  input  B,
  input  COUT
);

  xor xor_1 (SUM, A, B);
  and and_1 (COUT, A, B);
endmodule

module HALF_SUBTRACTOR (
  input  A,
  input  DIFF,
  input  B,
  input  COUT
);

  wire not_1_out;

  not not_1 (not_1_out, A);
  and and_1 (COUT, not_1_out, B);
  xor xor_1 (DIFF, A, B);
endmodule

module FULL_SUBTRACTOR (
  input  A,
  input  B,
  input  CIN,
  output DIFF,
  output COUT
);

  wire and_1_out, and_2_out, and_3_out, not_1_out;

  not not_1 (not_1_out, A);
  and and_1 (and_1_out, B, CIN);
  and and_2 (and_2_out, not_1_out, B);
  and and_3 (and_3_out, not_1_out, CIN);
  ExactlyOne xor_1 (.out(DIFF), .in0(A), .in1(B), .in2(CIN));
  or or_1 (COUT, and_1_out, and_2_out, and_3_out);
endmodule

module EIGHT_BIT_ADD_SUB (
  input  [7:0] A,
  input  [7:0] B,
  input  K,
  input  CIN,
  output COUT,
  output [7:0] SUM
);

  wire full_adder_1_p2, full_adder_2_p2, full_adder_3_p2, full_adder_4_p2, full_adder_5_p2, full_adder_6_p2,
       full_adder_7_p2, xor_1_out, xor_2_out, xor_3_out, xor_4_out, xor_5_out, xor_6_out, xor_7_out,
       xor_8_out;

  xor xor_1 (xor_1_out, K, B[0]);
  // FULL_ADDER full_adder_1: pin names not known; wires that end beside it: SUM[7], full_adder_1_p2
  xor xor_2 (xor_2_out, K, B[1]);
  // FULL_ADDER full_adder_2: pin names not known; wires that end beside it: SUM[6], full_adder_2_p2
  xor xor_3 (xor_3_out, K, B[2]);
  // FULL_ADDER full_adder_3: pin names not known; wires that end beside it: SUM[5], full_adder_3_p2
  xor xor_4 (xor_4_out, K, B[3]);
  // FULL_ADDER full_adder_4: pin names not known; wires that end beside it: SUM[4], full_adder_4_p2
  xor xor_5 (xor_5_out, K, B[4]);
  // FULL_ADDER full_adder_5: pin names not known; wires that end beside it: SUM[3], full_adder_5_p2
  xor xor_6 (xor_6_out, K, B[5]);
  // FULL_ADDER full_adder_6: pin names not known; wires that end beside it: SUM[2], full_adder_6_p2
  xor xor_7 (xor_7_out, K, B[6]);
  // FULL_ADDER full_adder_7: pin names not known; wires that end beside it: SUM[1], full_adder_7_p2
  xor xor_8 (xor_8_out, K, B[7]);
  // FULL_ADDER full_adder_8: pin names not known; wires that end beside it: SUM[0], COUT
endmodule

module MULT_HELPER (
  input  [15:0] A,
  input  B,
  output [15:0] F1,
  output [15:0] F2
);

  Multiplexer #(.width(16)) multiplexer_1 (.in0({16{1'b0}}), .in1({A[14:0], 1'b0}), .out(F1), .sel(B));

  assign F2 = {A[14:0], 1'b0};
endmodule

module EIGHT_BIT_MULT (
  input  [7:0] A,
  input  [7:0] B,
  output [15:0] out_3
);

  wire adder_1_cout, adder_2_cout, adder_3_cout, adder_4_cout, adder_5_cout, adder_6_cout, adder_7_cout;
  wire [15:0] adder_1_out, adder_2_out, adder_3_out, adder_4_out, adder_5_out, adder_6_out, adder_7_out,
       mult_helper_1_f1, mult_helper_1_f2, mult_helper_2_f1, mult_helper_2_f2, mult_helper_3_f1,
       mult_helper_3_f2, mult_helper_4_f1, mult_helper_4_f2, mult_helper_5_f1, mult_helper_5_f2,
       mult_helper_6_f1, mult_helper_6_f2, mult_helper_7_f1, multiplexer_1_out;

  Multiplexer #(.width(16)) multiplexer_1 (.in0({16{1'b0}}), .in1({{8{1'b0}}, A}), .out(multiplexer_1_out), .sel(B[0]));
  MULT_HELPER mult_helper_1 (.A({{8{1'b0}}, A}), .B(B[1]), .F1(mult_helper_1_f1), .F2(mult_helper_1_f2));
  MULT_HELPER mult_helper_2 (.A(mult_helper_1_f2), .B(B[2]), .F1(mult_helper_2_f1), .F2(mult_helper_2_f2));
  MULT_HELPER mult_helper_3 (.A(mult_helper_2_f2), .B(B[3]), .F1(mult_helper_3_f1), .F2(mult_helper_3_f2));
  MULT_HELPER mult_helper_4 (.A(mult_helper_3_f2), .B(B[4]), .F1(mult_helper_4_f1), .F2(mult_helper_4_f2));
  MULT_HELPER mult_helper_5 (.A(mult_helper_4_f2), .B(B[5]), .F1(mult_helper_5_f1), .F2(mult_helper_5_f2));
  MULT_HELPER mult_helper_6 (.A(mult_helper_5_f2), .B(B[6]), .F1(mult_helper_6_f1), .F2(mult_helper_6_f2));
  MULT_HELPER mult_helper_7 (.A(mult_helper_6_f2), .B(B[7]), .F1(mult_helper_7_f1));  // open: F2
  Adder #(.width(16)) adder_1 (
    .a(multiplexer_1_out), .b({16{1'b0}}), .out(adder_1_out), .cout(adder_1_cout));  // open: cin
  Adder #(.width(16)) adder_2 (
    .a(mult_helper_1_f1), .b(adder_1_out), .out(adder_2_out), .cin(adder_1_cout), .cout(adder_2_cout));
  Adder #(.width(16)) adder_3 (
    .a(adder_2_out), .b(mult_helper_2_f1), .out(adder_3_out), .cin(adder_2_cout), .cout(adder_3_cout));
  Adder #(.width(16)) adder_4 (
    .a(adder_3_out), .b(mult_helper_3_f1), .out(adder_4_out), .cin(adder_3_cout), .cout(adder_4_cout));
  Adder #(.width(16)) adder_5 (
    .a(adder_4_out), .b(mult_helper_4_f1), .out(adder_5_out), .cin(adder_4_cout), .cout(adder_5_cout));
  Adder #(.width(16)) adder_6 (
    .a(adder_5_out), .b(mult_helper_5_f1), .out(adder_6_out), .cin(adder_5_cout), .cout(adder_6_cout));
  Adder #(.width(16)) adder_7 (
    .a(adder_6_out), .b(mult_helper_6_f1), .out(adder_7_out), .cin(adder_6_cout), .cout(adder_7_cout));
  Adder #(.width(16)) adder_8 (.a(adder_7_out), .b(mult_helper_7_f1), .out(out_3), .cin(adder_7_cout));  // open: cout
endmodule

module EIGHT_SHIFT_LEFT (
  input  [7:0] in_1,
  output [7:0] out_2
);


  assign out_2 = {in_1[6:0], 1'b0};
endmodule

module LOGICAL_RIGHT_SHIFT (
  input  [3:0] A,
  input  [1:0] SHIFT,
  output [3:0] O
);

  Multiplexer #(.select(2), .width(4)) multiplexer_1 (
    .in0(A), .in1({1'b0, A[3:1]}), .in2({2'b00, A[3:2]}), .in3({3'b000, A[3]}), .out(O), .sel(SHIFT));
endmodule

module LOGICAL_LEFT_SHIFT (
  input  [3:0] A,
  input  [1:0] SHIFT,
  output [3:0] O
);

  Multiplexer #(.select(2), .width(4)) multiplexer_1 (
    .in0(A), .in1({A[2:0], 1'b0}), .in2({A[1:0], 2'b00}), .in3({A[0], 3'b000}), .out(O), .sel(SHIFT));
endmodule

module ROTATE_RIGHT_SHIFT (
  input  [3:0] A,
  input  [1:0] SHIFT,
  output [3:0] O
);

  Multiplexer #(.select(2), .width(4)) multiplexer_1 (
    .in0(A), .in1({A[0], A[3:1]}), .in2({A[1:0], A[3:2]}), .in3({A[2:0], A[3]}), .out(O), .sel(SHIFT));
endmodule

module ROTATE_LEFT_SHIFT (
  input  [3:0] A,
  input  [1:0] SHIFT,
  output [3:0] O
);

  Multiplexer #(.select(2), .width(4)) multiplexer_1 (
    .in0(A), .in1({A[2:0], A[3]}), .in2({A[1:0], A[3:2]}), .in3({A[0], A[3:1]}), .out(O), .sel(SHIFT));
endmodule

module SHIFT_RIGHT_ARTHMETRIC (
  input  [3:0] A,
  input  [1:0] SHIFT,
  output [3:0] O
);

  Multiplexer #(.select(2), .width(4)) multiplexer_1 (
    .in0(A), .in1({{2{A[3]}}, A[2:1]}), .in2({A[3], 1'b0, A[3:2]}), .in3({A[3], 2'b00, A[3]}), .out(O),
    .sel(SHIFT));
endmodule

module EIGHT_BIT_DIVISION (
  input  [7:0] A,
  input  [7:0] B,
  output [7:0] Remainder,
  output [7:0] Quotient
);

  wire [7:0] division_helper_1_aa, division_helper_1_d, division_helper_2_aa, division_helper_2_d,
       division_helper_3_aa, division_helper_3_d, division_helper_4_aa, division_helper_4_d,
       division_helper_5_aa, division_helper_5_d, division_helper_6_aa, division_helper_6_d,
       division_helper_7_aa, division_helper_7_d, division_helper_8_aa, division_helper_8_d,
       multiplexer_1_out, multiplexer_2_out, multiplexer_3_out, multiplexer_4_out, multiplexer_5_out,
       multiplexer_7_out;
  wire [7:1] multiplexer_6_out_2;
  wire [7:7] multiplexer_6_out;

  Multiplexer #(.width(8)) multiplexer_1 (
    .in0(division_helper_1_aa), .in1(division_helper_1_d), .out(multiplexer_1_out), .sel(Quotient[7]));
  DIVISION_HELPER division_helper_1 (
    .A({{7{1'b0}}, A[7]}), .B(B), .D(division_helper_1_d), .COUT(Quotient[7]), .AA(division_helper_1_aa));
  Multiplexer #(.width(8)) multiplexer_2 (
    .in0(division_helper_2_aa), .in1(division_helper_2_d), .out(multiplexer_2_out), .sel(Quotient[6]));
  DIVISION_HELPER division_helper_2 (
    .A({multiplexer_1_out[6:0], A[6]}), .B(B), .D(division_helper_2_d), .COUT(Quotient[6]),
    .AA(division_helper_2_aa));
  Multiplexer #(.width(8)) multiplexer_3 (
    .in0(division_helper_3_aa), .in1(division_helper_3_d), .out(multiplexer_3_out), .sel(Quotient[5]));
  DIVISION_HELPER division_helper_3 (
    .A({multiplexer_2_out[6:0], A[5]}), .B(B), .D(division_helper_3_d), .COUT(Quotient[5]),
    .AA(division_helper_3_aa));
  Multiplexer #(.width(8)) multiplexer_4 (
    .in0(division_helper_4_aa), .in1(division_helper_4_d), .out(multiplexer_4_out), .sel(Quotient[4]));
  DIVISION_HELPER division_helper_4 (
    .A({multiplexer_3_out[6:0], A[4]}), .B(B), .D(division_helper_4_d), .COUT(Quotient[4]),
    .AA(division_helper_4_aa));
  DIVISION_HELPER division_helper_5 (
    .A({multiplexer_4_out[6:0], A[3]}), .B(B), .D(division_helper_5_d), .COUT(Quotient[3]),
    .AA(division_helper_5_aa));
  Multiplexer #(.width(8)) multiplexer_5 (
    .in0(division_helper_5_aa), .in1(division_helper_5_d), .out(multiplexer_5_out), .sel(Quotient[3]));
  DIVISION_HELPER division_helper_6 (
    .A({multiplexer_5_out[6:0], A[2]}), .B(B), .D(division_helper_6_d), .COUT(Quotient[2]),
    .AA(division_helper_6_aa));
  Multiplexer #(.width(8)) multiplexer_6 (
    .in0(division_helper_6_aa), .in1(division_helper_6_d), .out({multiplexer_6_out[7], multiplexer_6_out_2}),
    .sel(Quotient[2]));
  Multiplexer #(.width(8)) multiplexer_7 (
    .in0(division_helper_7_aa), .in1(division_helper_7_d), .out(multiplexer_7_out), .sel(Quotient[1]));
  DIVISION_HELPER division_helper_7 (
    .A({multiplexer_6_out_2, A[1]}), .B(B), .D(division_helper_7_d), .COUT(Quotient[1]),
    .AA(division_helper_7_aa));
  Multiplexer #(.width(8)) multiplexer_8 (
    .in0(division_helper_8_aa), .in1(division_helper_8_d), .out(Remainder), .sel(Quotient[0]));
  DIVISION_HELPER division_helper_8 (
    .A({multiplexer_7_out[6:0], A[0]}), .B(B), .D(division_helper_8_d), .COUT(Quotient[0]),
    .AA(division_helper_8_aa));
endmodule

module DIVISION_HELPER (
  input  [7:0] B,
  input  [7:0] A,
  output [7:0] D,
  output COUT,
  output [7:0] AA
);

  wire subtractor_1_bout;

  Subtractor subtractor_1 (.a(A), .b(B), .out(D), .bout(subtractor_1_bout));  // open: bin
  not not_1 (COUT, subtractor_1_bout);

  assign AA = A;
endmodule

module EIGHT_BIT_COMPARATOR (
  input  [7:0] B,
  input  [7:0] A,
  output Greater,
  output Greater_OR_Equal,
  output Equal,
  output Less_OR_Equal,
  output Less
);

  wire and_1_out, and_2_out, and_3_out, and_4_out, and_5_out, and_6_out, and_7_out, and_8_out, and_9_out,
       and_10_out, and_11_out, and_12_out, and_13_out, and_14_out, and_15_out, and_16_out,
       comparator_helper_1_a_greater, comparator_helper_1_b_greater, comparator_helper_2_a_greater,
       comparator_helper_2_b_greater, comparator_helper_3_a_greater, comparator_helper_3_b_greater,
       comparator_helper_4_a_greater, comparator_helper_4_b_greater, comparator_helper_5_a_greater,
       comparator_helper_5_b_greater, comparator_helper_6_a_greater, comparator_helper_6_b_greater,
       not_1_out, not_2_out, not_3_out, not_4_out, not_5_out, not_6_out, not_7_out, not_8_out, not_9_out,
       not_10_out, not_11_out, not_12_out, not_13_out, not_14_out, not_15_out, not_16_out;

  not not_1 (not_1_out, B[7]);
  not not_2 (not_2_out, A[7]);
  not not_3 (not_3_out, B[6]);
  not not_4 (not_4_out, A[6]);
  not not_5 (not_5_out, B[5]);
  not not_6 (not_6_out, A[5]);
  not not_7 (not_7_out, B[4]);
  not not_8 (not_8_out, A[4]);
  not not_9 (not_9_out, B[3]);
  not not_10 (not_10_out, A[3]);
  not not_11 (not_11_out, B[2]);
  not not_12 (not_12_out, A[2]);
  not not_13 (not_13_out, B[1]);
  not not_14 (not_14_out, A[1]);
  not not_15 (not_15_out, B[0]);
  not not_16 (not_16_out, A[0]);
  and and_1 (and_1_out, not_1_out, A[7]);
  and and_2 (and_2_out, B[7], not_2_out);
  and and_3 (and_3_out, not_3_out, A[6]);
  and and_4 (and_4_out, B[6], not_4_out);
  and and_5 (and_5_out, not_5_out, A[5]);
  and and_6 (and_6_out, B[5], not_6_out);
  and and_7 (and_7_out, not_7_out, A[4]);
  and and_8 (and_8_out, B[4], not_8_out);
  and and_9 (and_9_out, not_9_out, A[3]);
  and and_10 (and_10_out, B[3], not_10_out);
  and and_11 (and_11_out, not_11_out, A[2]);
  and and_12 (and_12_out, B[2], not_12_out);
  and and_13 (and_13_out, not_13_out, A[1]);
  and and_14 (and_14_out, B[1], not_14_out);
  and and_15 (and_15_out, not_15_out, A[0]);
  and and_16 (and_16_out, B[0], not_16_out);
  COMPARATOR_HELPER comparator_helper_1 (
    .A_G(and_1_out), .B_G(and_2_out), .A_GG(and_3_out), .B_GG(and_4_out),
    .A_GREATER(comparator_helper_1_a_greater), .B_GREATER(comparator_helper_1_b_greater));
  COMPARATOR_HELPER comparator_helper_2 (
    .A_G(and_5_out), .B_G(and_6_out), .A_GG(and_7_out), .B_GG(and_8_out),
    .A_GREATER(comparator_helper_2_a_greater), .B_GREATER(comparator_helper_2_b_greater));
  COMPARATOR_HELPER comparator_helper_3 (
    .A_G(and_9_out), .B_G(and_10_out), .A_GG(and_11_out), .B_GG(and_12_out),
    .A_GREATER(comparator_helper_3_a_greater), .B_GREATER(comparator_helper_3_b_greater));
  COMPARATOR_HELPER comparator_helper_4 (
    .A_G(and_13_out), .B_G(and_14_out), .A_GG(and_15_out), .B_GG(and_16_out),
    .A_GREATER(comparator_helper_4_a_greater), .B_GREATER(comparator_helper_4_b_greater));
  COMPARATOR_HELPER comparator_helper_5 (
    .A_G(comparator_helper_1_a_greater), .B_G(comparator_helper_1_b_greater),
    .A_GG(comparator_helper_2_a_greater), .B_GG(comparator_helper_2_b_greater),
    .A_GREATER(comparator_helper_5_a_greater), .B_GREATER(comparator_helper_5_b_greater));
  COMPARATOR_HELPER comparator_helper_6 (
    .A_G(comparator_helper_3_a_greater), .B_G(comparator_helper_3_b_greater),
    .A_GG(comparator_helper_4_a_greater), .B_GG(comparator_helper_4_b_greater),
    .A_GREATER(comparator_helper_6_a_greater), .B_GREATER(comparator_helper_6_b_greater));
  COMPARATOR_HELPER comparator_helper_7 (
    .A_G(comparator_helper_5_a_greater), .B_G(comparator_helper_5_b_greater),
    .A_GG(comparator_helper_6_a_greater), .B_GG(comparator_helper_6_b_greater), .A_GREATER(Greater),
    .B_GREATER(Less));
  nand nand_1 (Equal, Greater, Less);
  or or_1 (Greater_OR_Equal, Greater, Equal);
  or or_2 (Less_OR_Equal, Equal, Less);
endmodule

module COMPARATOR_HELPER (
  input  A_G,
  input  B_G,
  input  A_GG,
  input  B_GG,
  output A_GREATER,
  output B_GREATER
);

  wire and_1_out, and_2_out, and_3_out, and_4_out, and_5_out, not_1_out, not_2_out, not_3_out, not_4_out;

  not not_1 (not_1_out, A_G);
  not not_2 (not_2_out, B_G);
  not not_3 (not_3_out, A_GG);
  not not_4 (not_4_out, B_GG);
  and and_1 (and_1_out, A_GG, not_4_out);
  and and_2 (and_2_out, A_G, not_2_out);
  and and_3 (and_3_out, not_1_out, not_3_out, B_GG);
  and and_4 (and_4_out, not_1_out, B_G);
  and and_5 (and_5_out, B_G, not_3_out, B_GG);
  or or_1 (A_GREATER, and_1_out, and_2_out);
  or or_2 (B_GREATER, and_3_out, and_4_out, and_5_out);
endmodule

module EIGHT_BIT_REGISTER (
  input  Clock,
  input  Enable,
  input  [7:0] Data,
  output [7:0] O
);

  wire and_1_out;

  and and_1 (and_1_out, Clock, Enable);
  D_Flip_Flop d_ff_1 (.clk(and_1_out), .D(Data[0]), .Q(O[0]));  // open: Qn, preset, reset
  D_Flip_Flop d_ff_2 (.clk(and_1_out), .D(Data[1]), .Q(O[1]));  // open: Qn, preset, reset
  D_Flip_Flop d_ff_3 (.clk(and_1_out), .D(Data[2]), .Q(O[2]));  // open: Qn, preset, reset
  D_Flip_Flop d_ff_4 (.clk(and_1_out), .D(Data[3]), .Q(O[3]));  // open: Qn, preset, reset
  D_Flip_Flop d_ff_5 (.clk(and_1_out), .D(Data[4]), .Q(O[4]));  // open: Qn, preset, reset
  D_Flip_Flop d_ff_6 (.clk(and_1_out), .D(Data[5]), .Q(O[5]));  // open: Qn, preset, reset
  D_Flip_Flop d_ff_7 (.clk(and_1_out), .D(Data[6]), .Q(O[6]));  // open: Qn, preset, reset
  D_Flip_Flop d_ff_8 (.clk(and_1_out), .D(Data[7]), .Q(O[7]));  // open: Qn, preset, reset
endmodule

module SIXTEENxSEXTEEN_REGISTER (
  input  [3:0] Address,
  input  [15:0] Data,
  input  Enable,
  input  Clock,
  output [15:0] Outputs
);

  wire demultiplexer_1_out0, demultiplexer_1_out1, demultiplexer_1_out2, demultiplexer_1_out3,
       demultiplexer_1_out4, demultiplexer_1_out5, demultiplexer_1_out6, demultiplexer_1_out7,
       demultiplexer_1_out8, demultiplexer_1_out9, demultiplexer_1_out10, demultiplexer_1_out11,
       demultiplexer_1_out12, demultiplexer_1_out13, demultiplexer_1_out14, demultiplexer_1_out15;
  wire [15:0] register_1_q, register_2_q, register_3_q, register_4_q, register_5_q, register_6_q,
       register_7_q, register_8_q, register_9_q, register_10_q, register_11_q, register_12_q, register_13_q,
       register_14_q, register_15_q, register_16_q;

  Demultiplexer #(.select(4)) demultiplexer_1 (
    .out0(demultiplexer_1_out0), .out1(demultiplexer_1_out1), .out2(demultiplexer_1_out2),
    .out3(demultiplexer_1_out3), .out4(demultiplexer_1_out4), .out5(demultiplexer_1_out5),
    .out6(demultiplexer_1_out6), .out7(demultiplexer_1_out7), .out8(demultiplexer_1_out8),
    .out9(demultiplexer_1_out9), .out10(demultiplexer_1_out10), .out11(demultiplexer_1_out11),
    .out12(demultiplexer_1_out12), .out13(demultiplexer_1_out13), .out14(demultiplexer_1_out14),
    .out15(demultiplexer_1_out15), .in(Enable), .sel(Address));
  Register #(.width(16)) register_1 (.D(Data), .en(demultiplexer_1_out0), .clk(Clock), .Q(register_1_q));  // open: clr
  Register #(.width(16)) register_2 (.D(Data), .en(demultiplexer_1_out1), .clk(Clock), .Q(register_2_q));  // open: clr
  Register #(.width(16)) register_3 (.D(Data), .en(demultiplexer_1_out2), .clk(Clock), .Q(register_3_q));  // open: clr
  Register #(.width(16)) register_4 (.D(Data), .en(demultiplexer_1_out3), .clk(Clock), .Q(register_4_q));  // open: clr
  Register #(.width(16)) register_5 (.D(Data), .en(demultiplexer_1_out4), .clk(Clock), .Q(register_5_q));  // open: clr
  Register #(.width(16)) register_6 (.D(Data), .en(demultiplexer_1_out5), .clk(Clock), .Q(register_6_q));  // open: clr
  Register #(.width(16)) register_7 (.D(Data), .en(demultiplexer_1_out6), .clk(Clock), .Q(register_7_q));  // open: clr
  Register #(.width(16)) register_8 (.D(Data), .en(demultiplexer_1_out7), .clk(Clock), .Q(register_8_q));  // open: clr
  Register #(.width(16)) register_9 (.D(Data), .en(demultiplexer_1_out8), .clk(Clock), .Q(register_9_q));  // open: clr
  Register #(.width(16)) register_10 (
    .D(Data), .en(demultiplexer_1_out9), .clk(Clock), .Q(register_10_q));  // open: clr
  Register #(.width(16)) register_11 (
    .D(Data), .en(demultiplexer_1_out10), .clk(Clock), .Q(register_11_q));  // open: clr
  Register #(.width(16)) register_12 (
    .D(Data), .en(demultiplexer_1_out11), .clk(Clock), .Q(register_12_q));  // open: clr
  Register #(.width(16)) register_13 (
    .D(Data), .en(demultiplexer_1_out12), .clk(Clock), .Q(register_13_q));  // open: clr
  Register #(.width(16)) register_14 (
    .D(Data), .en(demultiplexer_1_out13), .clk(Clock), .Q(register_14_q));  // open: clr
  Register #(.width(16)) register_15 (
    .D(Data), .en(demultiplexer_1_out14), .clk(Clock), .Q(register_15_q));  // open: clr
  Register #(.width(16)) register_16 (
    .D(Data), .en(demultiplexer_1_out15), .clk(Clock), .Q(register_16_q));  // open: clr
  Multiplexer #(.select(4), .width(16)) multiplexer_1 (
    .in0(register_1_q), .in1(register_2_q), .in2(register_3_q), .in3(register_4_q), .in4(register_5_q),
    .in5(register_6_q), .in6(register_7_q), .in7(register_8_q), .in8(register_9_q), .in9(register_10_q),
    .in10(register_11_q), .in11(register_12_q), .in12(register_13_q), .in13(register_14_q),
    .in14(register_15_q), .in15(register_16_q), .out(Outputs), .sel(Address));
endmodule

module TWOFIFTYSIXxEIGHT_REGISTER (
  input  [7:0] Address,
  input  [7:0] Data,
  input  ENABLE_READ,
  input  ENABLE_WRITE,
  input  CLOCK,
  output [7:0] Outputs
);

  wire and_1_out, demultiplexer_1_out0, demultiplexer_1_out1, demultiplexer_1_out2, demultiplexer_1_out3,
       demultiplexer_1_out4, demultiplexer_1_out5, demultiplexer_1_out6, demultiplexer_1_out7,
       demultiplexer_1_out8, demultiplexer_1_out9, demultiplexer_1_out10, demultiplexer_1_out11,
       demultiplexer_1_out12, demultiplexer_1_out13, demultiplexer_1_out14, demultiplexer_1_out15;
  wire [7:0] multiplexer_1_out, sixteenxsexteen_register_1_p5, sixteenxsexteen_register_2_p5,
       sixteenxsexteen_register_3_p5, sixteenxsexteen_register_4_p5, sixteenxsexteen_register_5_p5,
       sixteenxsexteen_register_6_p5, sixteenxsexteen_register_7_p5, sixteenxsexteen_register_8_p5,
       sixteenxsexteen_register_9_p5, sixteenxsexteen_register_10_p5, sixteenxsexteen_register_11_p5,
       sixteenxsexteen_register_12_p5, sixteenxsexteen_register_13_p5, sixteenxsexteen_register_14_p5,
       sixteenxsexteen_register_15_p5, sixteenxsexteen_register_16_p5;

  and and_1 (and_1_out, ENABLE_WRITE, ENABLE_READ);
  Demultiplexer #(.select(4)) demultiplexer_1 (
    .out0(demultiplexer_1_out0), .out1(demultiplexer_1_out1), .out2(demultiplexer_1_out2),
    .out3(demultiplexer_1_out3), .out4(demultiplexer_1_out4), .out5(demultiplexer_1_out5),
    .out6(demultiplexer_1_out6), .out7(demultiplexer_1_out7), .out8(demultiplexer_1_out8),
    .out9(demultiplexer_1_out9), .out10(demultiplexer_1_out10), .out11(demultiplexer_1_out11),
    .out12(demultiplexer_1_out12), .out13(demultiplexer_1_out13), .out14(demultiplexer_1_out14),
    .out15(demultiplexer_1_out15), .in(and_1_out), .sel(Address[7:4]));
  // SIXTEENxSEXTEEN_REGISTER sixteenxsexteen_register_1: pin names not known; wires that end beside it: Address[3:0], Data, demultiplexer_1_out0, CLOCK, sixteenxsexteen_register_1_p5
  // SIXTEENxSEXTEEN_REGISTER sixteenxsexteen_register_2: pin names not known; wires that end beside it: Address[3:0], Data, demultiplexer_1_out1, CLOCK, sixteenxsexteen_register_2_p5
  // SIXTEENxSEXTEEN_REGISTER sixteenxsexteen_register_3: pin names not known; wires that end beside it: Address[3:0], Data, demultiplexer_1_out2, CLOCK, sixteenxsexteen_register_3_p5
  // SIXTEENxSEXTEEN_REGISTER sixteenxsexteen_register_4: pin names not known; wires that end beside it: Address[3:0], Data, demultiplexer_1_out3, CLOCK, sixteenxsexteen_register_4_p5
  // SIXTEENxSEXTEEN_REGISTER sixteenxsexteen_register_5: pin names not known; wires that end beside it: Address[3:0], Data, demultiplexer_1_out4, CLOCK, sixteenxsexteen_register_5_p5
  // SIXTEENxSEXTEEN_REGISTER sixteenxsexteen_register_6: pin names not known; wires that end beside it: Address[3:0], Data, demultiplexer_1_out5, CLOCK, sixteenxsexteen_register_6_p5
  // SIXTEENxSEXTEEN_REGISTER sixteenxsexteen_register_7: pin names not known; wires that end beside it: Address[3:0], Data, demultiplexer_1_out6, CLOCK, sixteenxsexteen_register_7_p5
  // SIXTEENxSEXTEEN_REGISTER sixteenxsexteen_register_8: pin names not known; wires that end beside it: Address[3:0], Data, demultiplexer_1_out7, CLOCK, sixteenxsexteen_register_8_p5
  // SIXTEENxSEXTEEN_REGISTER sixteenxsexteen_register_9: pin names not known; wires that end beside it: Address[3:0], Data, demultiplexer_1_out8, CLOCK, sixteenxsexteen_register_9_p5
  // SIXTEENxSEXTEEN_REGISTER sixteenxsexteen_register_10: pin names not known; wires that end beside it: Address[3:0], Data, demultiplexer_1_out9, CLOCK, sixteenxsexteen_register_10_p5
  // SIXTEENxSEXTEEN_REGISTER sixteenxsexteen_register_11: pin names not known; wires that end beside it: Address[3:0], Data, demultiplexer_1_out10, CLOCK, sixteenxsexteen_register_11_p5
  // SIXTEENxSEXTEEN_REGISTER sixteenxsexteen_register_12: pin names not known; wires that end beside it: Address[3:0], Data, demultiplexer_1_out11, CLOCK, sixteenxsexteen_register_12_p5
  // SIXTEENxSEXTEEN_REGISTER sixteenxsexteen_register_13: pin names not known; wires that end beside it: Address[3:0], Data, demultiplexer_1_out12, CLOCK, sixteenxsexteen_register_13_p5
  // SIXTEENxSEXTEEN_REGISTER sixteenxsexteen_register_14: pin names not known; wires that end beside it: Address[3:0], Data, demultiplexer_1_out13, CLOCK, sixteenxsexteen_register_14_p5
  // SIXTEENxSEXTEEN_REGISTER sixteenxsexteen_register_15: pin names not known; wires that end beside it: Address[3:0], Data, demultiplexer_1_out14, CLOCK, sixteenxsexteen_register_15_p5
  // SIXTEENxSEXTEEN_REGISTER sixteenxsexteen_register_16: pin names not known; wires that end beside it: Address[3:0], Data, demultiplexer_1_out15, CLOCK, sixteenxsexteen_register_16_p5
  Multiplexer #(.select(4), .width(8)) multiplexer_1 (
    .in0(sixteenxsexteen_register_1_p5), .in1(sixteenxsexteen_register_2_p5),
    .in2(sixteenxsexteen_register_3_p5), .in3(sixteenxsexteen_register_4_p5),
    .in4(sixteenxsexteen_register_5_p5), .in5(sixteenxsexteen_register_6_p5),
    .in6(sixteenxsexteen_register_7_p5), .in7(sixteenxsexteen_register_8_p5),
    .in8(sixteenxsexteen_register_9_p5), .in9(sixteenxsexteen_register_10_p5),
    .in10(sixteenxsexteen_register_11_p5), .in11(sixteenxsexteen_register_12_p5),
    .in12(sixteenxsexteen_register_13_p5), .in13(sixteenxsexteen_register_14_p5),
    .in14(sixteenxsexteen_register_15_p5), .in15(sixteenxsexteen_register_16_p5), .out(multiplexer_1_out),
    .sel(Address[7:4]));
  Multiplexer #(.width(8)) multiplexer_2 (.in0({8{1'b0}}), .in1(multiplexer_1_out), .out(Outputs), .sel(ENABLE_READ));
endmodule

module SIXTEEN_BIT_PROGRAM_COUNTER (
  input  CLOCK,
  input  RESET,
  input  WRITE,
  input  [15:0] INP,
  output [15:0] COUNT
);

  wire and_1_out, and_2_out, and_3_out, and_4_out, and_5_out, and_6_out, and_7_out, and_8_out, and_9_out,
       and_10_out, and_11_out, and_12_out, and_13_out, and_14_out, and_15_out, and_16_out, and_17_out,
       and_18_out, and_19_out, and_20_out, and_21_out, and_22_out, and_23_out, and_24_out, and_25_out,
       and_26_out, and_27_out, and_28_out, and_29_out, and_30_out, and_31_out, and_32_out, d_ff_1_qn,
       d_ff_2_qn, d_ff_3_qn, d_ff_4_qn, d_ff_5_qn, d_ff_6_qn, d_ff_7_qn, d_ff_8_qn, d_ff_9_qn, d_ff_10_qn,
       d_ff_11_qn, d_ff_12_qn, d_ff_13_qn, d_ff_14_qn, d_ff_15_qn, d_ff_16_qn, or_1_out, or_2_out, or_3_out,
       or_4_out, or_5_out, or_6_out, or_7_out, or_8_out, or_9_out, or_10_out, or_11_out, or_12_out,
       or_13_out, or_14_out, or_15_out, or_16_out;

  and and_1 (and_1_out, WRITE, INP[0]);
  and and_2 (and_2_out, WRITE, ~INP[0]);  // AND_Gate
  and and_3 (and_3_out, WRITE, INP[1]);
  and and_4 (and_4_out, WRITE, ~INP[1]);  // AND_Gate
  and and_5 (and_5_out, WRITE, INP[2]);
  and and_6 (and_6_out, WRITE, ~INP[2]);  // AND_Gate
  and and_7 (and_7_out, WRITE, INP[3]);
  and and_8 (and_8_out, WRITE, ~INP[3]);  // AND_Gate
  and and_9 (and_9_out, WRITE, INP[4]);
  and and_10 (and_10_out, WRITE, ~INP[4]);  // AND_Gate
  and and_11 (and_11_out, WRITE, INP[5]);
  and and_12 (and_12_out, WRITE, ~INP[5]);  // AND_Gate
  and and_13 (and_13_out, WRITE, INP[6]);
  and and_14 (and_14_out, WRITE, ~INP[6]);  // AND_Gate
  and and_15 (and_15_out, WRITE, INP[7]);
  and and_16 (and_16_out, WRITE, ~INP[7]);  // AND_Gate
  and and_17 (and_17_out, WRITE, INP[8]);
  and and_18 (and_18_out, WRITE, ~INP[8]);  // AND_Gate
  and and_19 (and_19_out, WRITE, INP[9]);
  and and_20 (and_20_out, WRITE, ~INP[9]);  // AND_Gate
  and and_21 (and_21_out, WRITE, INP[10]);
  and and_22 (and_22_out, WRITE, ~INP[10]);  // AND_Gate
  and and_23 (and_23_out, WRITE, INP[11]);
  and and_24 (and_24_out, WRITE, ~INP[11]);  // AND_Gate
  and and_25 (and_25_out, WRITE, INP[12]);
  and and_26 (and_26_out, WRITE, ~INP[12]);  // AND_Gate
  and and_27 (and_27_out, WRITE, INP[13]);
  and and_28 (and_28_out, WRITE, ~INP[13]);  // AND_Gate
  and and_29 (and_29_out, WRITE, INP[14]);
  and and_30 (and_30_out, WRITE, ~INP[14]);  // AND_Gate
  and and_31 (and_31_out, WRITE, INP[15]);
  and and_32 (and_32_out, WRITE, ~INP[15]);  // AND_Gate
  D_Flip_Flop d_ff_1 (.D(d_ff_1_qn), .clk(CLOCK), .Q(COUNT[0]), .Qn(d_ff_1_qn), .preset(and_1_out), .reset(or_1_out));
  or or_1 (or_1_out, RESET, and_2_out);
  or or_2 (or_2_out, RESET, and_4_out);
  or or_3 (or_3_out, RESET, and_6_out);
  or or_4 (or_4_out, RESET, and_8_out);
  or or_5 (or_5_out, RESET, and_10_out);
  or or_6 (or_6_out, RESET, and_12_out);
  or or_7 (or_7_out, RESET, and_14_out);
  or or_8 (or_8_out, RESET, and_16_out);
  or or_9 (or_9_out, RESET, and_18_out);
  or or_10 (or_10_out, RESET, and_20_out);
  or or_11 (or_11_out, RESET, and_22_out);
  or or_12 (or_12_out, RESET, and_24_out);
  or or_13 (or_13_out, RESET, and_26_out);
  or or_14 (or_14_out, RESET, and_28_out);
  or or_15 (or_15_out, RESET, and_30_out);
  or or_16 (or_16_out, RESET, and_32_out);
  D_Flip_Flop d_ff_2 (
    .D(d_ff_2_qn), .clk(d_ff_1_qn), .Q(COUNT[1]), .Qn(d_ff_2_qn), .preset(and_3_out), .reset(or_2_out));
  D_Flip_Flop d_ff_3 (
    .D(d_ff_3_qn), .clk(d_ff_2_qn), .Q(COUNT[2]), .Qn(d_ff_3_qn), .preset(and_5_out), .reset(or_3_out));
  D_Flip_Flop d_ff_4 (
    .D(d_ff_4_qn), .clk(d_ff_3_qn), .Q(COUNT[3]), .Qn(d_ff_4_qn), .preset(and_7_out), .reset(or_4_out));
  D_Flip_Flop d_ff_5 (
    .D(d_ff_5_qn), .clk(d_ff_4_qn), .Q(COUNT[4]), .Qn(d_ff_5_qn), .preset(and_9_out), .reset(or_5_out));
  D_Flip_Flop d_ff_6 (
    .D(d_ff_6_qn), .clk(d_ff_5_qn), .Q(COUNT[5]), .Qn(d_ff_6_qn), .preset(and_11_out), .reset(or_6_out));
  D_Flip_Flop d_ff_7 (
    .D(d_ff_7_qn), .clk(d_ff_6_qn), .Q(COUNT[6]), .Qn(d_ff_7_qn), .preset(and_13_out), .reset(or_7_out));
  D_Flip_Flop d_ff_8 (
    .D(d_ff_8_qn), .clk(d_ff_7_qn), .Q(COUNT[7]), .Qn(d_ff_8_qn), .preset(and_15_out), .reset(or_8_out));
  D_Flip_Flop d_ff_9 (
    .D(d_ff_9_qn), .clk(d_ff_8_qn), .Q(COUNT[8]), .Qn(d_ff_9_qn), .preset(and_17_out), .reset(or_9_out));
  D_Flip_Flop d_ff_10 (
    .D(d_ff_10_qn), .clk(d_ff_9_qn), .Q(COUNT[9]), .Qn(d_ff_10_qn), .preset(and_19_out), .reset(or_10_out));
  D_Flip_Flop d_ff_11 (
    .D(d_ff_11_qn), .clk(d_ff_10_qn), .Q(COUNT[10]), .Qn(d_ff_11_qn), .preset(and_21_out), .reset(or_11_out));
  D_Flip_Flop d_ff_12 (
    .D(d_ff_12_qn), .clk(d_ff_11_qn), .Q(COUNT[11]), .Qn(d_ff_12_qn), .preset(and_23_out), .reset(or_12_out));
  D_Flip_Flop d_ff_13 (
    .D(d_ff_13_qn), .clk(d_ff_12_qn), .Q(COUNT[12]), .Qn(d_ff_13_qn), .preset(and_25_out), .reset(or_13_out));
  D_Flip_Flop d_ff_14 (
    .D(d_ff_14_qn), .clk(d_ff_13_qn), .Q(COUNT[13]), .Qn(d_ff_14_qn), .preset(and_27_out), .reset(or_14_out));
  D_Flip_Flop d_ff_15 (
    .D(d_ff_15_qn), .clk(d_ff_14_qn), .Q(COUNT[14]), .Qn(d_ff_15_qn), .preset(and_29_out), .reset(or_15_out));
  D_Flip_Flop d_ff_16 (
    .D(d_ff_16_qn), .clk(d_ff_15_qn), .Q(COUNT[15]), .Qn(d_ff_16_qn), .preset(and_31_out), .reset(or_16_out));
  Register #(.width(16)) register_1 (.D(COUNT), .en(CLOCK), .clk(CLOCK));  // open: Q, clr
endmodule

module TWO_BIT_CLOCK (
  input  CLOCK,
  input  RESET,
  output OUT1,
  output OUT2
);

  wire d_ff_1_qn, d_ff_2_q, not_1_out;

  D_Flip_Flop d_ff_1 (.D(d_ff_1_qn), .clk(CLOCK), .Q(OUT1), .Qn(d_ff_1_qn), .reset(RESET));  // open: preset
  not not_1 (not_1_out, CLOCK);
  D_Flip_Flop d_ff_2 (.D(OUT1), .clk(not_1_out), .Q(d_ff_2_q), .reset(RESET));  // open: Qn, preset
  and and_1 (OUT2, d_ff_2_q, d_ff_1_qn);
endmodule

module SIXTEEN_SIXTEEN_REGISTER (
  input  RESET,
  input  [3:0] WRITE_Address,
  input  [15:0] INPUT_Data,
  input  ENABLE,
  input  CLOCK,
  input  [3:0] INPUT_ADDRESS_A,
  input  [3:0] INPUT_ADDRESS_B,
  input  [15:0] TIME_INPUT,
  input  [15:0] USER_INPUT,
  output [15:0] OUTPUT_A,
  output [15:0] OUTPUT_B,
  output [15:0] BASE_POINTER
);

  wire and_1_out, demultiplexer_1_out0, demultiplexer_1_out1, demultiplexer_1_out2, demultiplexer_1_out3,
       demultiplexer_1_out4, demultiplexer_1_out5, demultiplexer_1_out6, demultiplexer_1_out7,
       demultiplexer_1_out8, demultiplexer_1_out9, demultiplexer_1_out10, demultiplexer_1_out11,
       demultiplexer_1_out12, demultiplexer_1_out13, demultiplexer_1_out14, demultiplexer_1_out15;
  wire [15:0] register_1_q, register_2_q, register_3_q, register_4_q, register_5_q, register_6_q,
       register_7_q, register_8_q, register_9_q, register_10_q, register_11_q, register_12_q, register_14_q;

  and and_1 (and_1_out, CLOCK, ENABLE);
  Demultiplexer #(.select(4)) demultiplexer_1 (
    .out0(demultiplexer_1_out0), .out1(demultiplexer_1_out1), .out2(demultiplexer_1_out2),
    .out3(demultiplexer_1_out3), .out4(demultiplexer_1_out4), .out5(demultiplexer_1_out5),
    .out6(demultiplexer_1_out6), .out7(demultiplexer_1_out7), .out8(demultiplexer_1_out8),
    .out9(demultiplexer_1_out9), .out10(demultiplexer_1_out10), .out11(demultiplexer_1_out11),
    .out12(demultiplexer_1_out12), .out13(demultiplexer_1_out13), .out14(demultiplexer_1_out14),
    .out15(demultiplexer_1_out15), .in(and_1_out), .sel(WRITE_Address));
  Register #(.width(16)) register_1 (
    .D(INPUT_Data), .en(demultiplexer_1_out0), .clk(demultiplexer_1_out0), .Q(register_1_q), .clr(RESET));
  Register #(.width(16)) register_2 (
    .D(INPUT_Data), .en(demultiplexer_1_out1), .clk(demultiplexer_1_out1), .Q(register_2_q), .clr(RESET));
  Register #(.width(16)) register_3 (
    .D(INPUT_Data), .en(demultiplexer_1_out2), .clk(demultiplexer_1_out2), .Q(register_3_q), .clr(RESET));
  Register #(.width(16)) register_4 (
    .D(INPUT_Data), .en(demultiplexer_1_out3), .clk(demultiplexer_1_out3), .Q(register_4_q), .clr(RESET));
  Register #(.width(16)) register_5 (
    .D(INPUT_Data), .en(demultiplexer_1_out4), .clk(demultiplexer_1_out4), .Q(register_5_q), .clr(RESET));
  Register #(.width(16)) register_6 (
    .D(INPUT_Data), .en(demultiplexer_1_out5), .clk(demultiplexer_1_out5), .Q(register_6_q), .clr(RESET));
  Register #(.width(16)) register_7 (
    .D(INPUT_Data), .en(demultiplexer_1_out6), .clk(demultiplexer_1_out6), .Q(register_7_q), .clr(RESET));
  Register #(.width(16)) register_8 (
    .D(INPUT_Data), .en(demultiplexer_1_out7), .clk(demultiplexer_1_out7), .Q(register_8_q), .clr(RESET));
  Register #(.width(16)) register_9 (
    .D(INPUT_Data), .en(demultiplexer_1_out8), .clk(demultiplexer_1_out8), .Q(register_9_q), .clr(RESET));
  Register #(.width(16)) register_10 (
    .D(INPUT_Data), .en(demultiplexer_1_out9), .clk(demultiplexer_1_out9), .Q(register_10_q), .clr(RESET));
  Register #(.width(16)) register_11 (
    .D(INPUT_Data), .en(demultiplexer_1_out10), .clk(demultiplexer_1_out10), .Q(register_11_q), .clr(RESET));
  Register #(.width(16)) register_12 (
    .D(INPUT_Data), .en(demultiplexer_1_out11), .clk(demultiplexer_1_out11), .Q(register_12_q), .clr(RESET));
  Register #(.width(16)) register_13 (
    .D(INPUT_Data), .en(demultiplexer_1_out14), .clk(demultiplexer_1_out14), .Q(BASE_POINTER), .clr(RESET));
  Register #(.width(16)) register_14 (
    .D(INPUT_Data), .en(demultiplexer_1_out15), .clk(demultiplexer_1_out15), .Q(register_14_q), .clr(RESET));
  Multiplexer #(.select(4), .width(16)) multiplexer_1 (
    .in0(register_1_q), .in1(register_2_q), .in2(register_3_q), .in3(register_4_q), .in4(register_5_q),
    .in5(register_6_q), .in6(register_7_q), .in7(register_8_q), .in8(register_9_q), .in9(register_10_q),
    .in10(register_11_q), .in11(register_12_q), .in12(TIME_INPUT), .in13(USER_INPUT), .in14(BASE_POINTER),
    .in15(register_14_q), .out(OUTPUT_A), .sel(INPUT_ADDRESS_A));
  Multiplexer #(.select(4), .width(16)) multiplexer_2 (
    .in0(register_1_q), .in1(register_2_q), .in2(register_3_q), .in3(register_4_q), .in4(register_5_q),
    .in5(register_6_q), .in6(register_7_q), .in7(register_8_q), .in8(register_9_q), .in9(register_10_q),
    .in10(register_11_q), .in11(register_12_q), .in12(TIME_INPUT), .in13(USER_INPUT), .in14(BASE_POINTER),
    .in15(register_14_q), .out(OUTPUT_B), .sel(INPUT_ADDRESS_B));
endmodule

module INC_DEC_FOUR_BIT_COUNTER (
  input  clk,
  input  shf,
  output [3:0] OUTPUTS,
  output BORROW,
  output CARRY
);

  wire and_3_out, and_4_out, and_5_out, and_6_out, and_7_out, and_8_out, and_9_out, and_10_out, and_11_out,
       and_12_out, and_13_out, and_14_out, and_15_out, and_16_out, and_17_out, and_18_out, and_19_out,
       and_20_out, and_21_out, and_22_out, not_1_out, not_2_out, not_3_out, not_4_out, not_5_out, not_6_out,
       or_1_out, or_2_out, or_3_out, or_4_out;
  wire [3:0] register_1_q;

  Register #(.width(4)) register_1 (.D(OUTPUTS), .clk(clk), .Q(register_1_q));  // open: en, clr
  D_Flip_Flop d_ff_1 (.D(or_1_out), .clk(clk), .Q(OUTPUTS[3]));  // open: Qn, preset, reset
  D_Flip_Flop d_ff_2 (.D(or_2_out), .clk(clk), .Q(OUTPUTS[2]));  // open: Qn, preset, reset
  D_Flip_Flop d_ff_3 (.D(or_3_out), .clk(clk), .Q(OUTPUTS[1]));  // open: Qn, preset, reset
  D_Flip_Flop d_ff_4 (.D(or_4_out), .clk(clk), .Q(OUTPUTS[0]));  // open: Qn, preset, reset
  and and_1 (BORROW, ~OUTPUTS[0], ~OUTPUTS[1], ~OUTPUTS[2], ~OUTPUTS[3], register_1_q[0], register_1_q[1], register_1_q[2], register_1_q[3]);  // AND_Gate
  and and_2 (CARRY, OUTPUTS[0], OUTPUTS[1], OUTPUTS[2], OUTPUTS[3], ~register_1_q[0], ~register_1_q[1], ~register_1_q[2], ~register_1_q[3]);  // AND_Gate
  not not_1 (not_1_out, OUTPUTS[3]);
  not not_2 (not_2_out, OUTPUTS[2]);
  not not_3 (not_3_out, OUTPUTS[1]);
  not not_4 (not_4_out, OUTPUTS[0]);
  not not_5 (not_5_out, 1'b1);
  not not_6 (not_6_out, shf);
  and and_3 (and_3_out, not_1_out, not_2_out, not_3_out, not_4_out, 1'b1, shf);
  and and_4 (and_4_out, not_1_out, OUTPUTS[2], OUTPUTS[1], OUTPUTS[0], 1'b1, not_6_out);
  and and_5 (and_5_out, OUTPUTS[3], not_5_out);
  and and_6 (and_6_out, OUTPUTS[3], OUTPUTS[2], not_3_out);
  and and_7 (and_7_out, OUTPUTS[3], not_4_out, not_6_out);
  and and_8 (and_8_out, OUTPUTS[3], not_2_out, OUTPUTS[0]);
  and and_9 (and_9_out, OUTPUTS[3], OUTPUTS[1], shf);
  and and_10 (and_10_out, not_2_out, not_3_out, not_4_out, 1'b1, shf);
  and and_11 (and_11_out, not_2_out, OUTPUTS[1], OUTPUTS[0], 1'b1, not_6_out);
  and and_12 (and_12_out, OUTPUTS[2], not_5_out);
  and and_13 (and_13_out, OUTPUTS[2], not_3_out, OUTPUTS[0]);
  and and_14 (and_14_out, OUTPUTS[2], not_4_out, not_6_out);
  and and_15 (and_15_out, OUTPUTS[2], OUTPUTS[1], shf);
  and and_16 (and_16_out, not_3_out, not_4_out, 1'b1, shf);
  and and_17 (and_17_out, not_3_out, OUTPUTS[0], 1'b1, not_6_out);
  and and_18 (and_18_out, OUTPUTS[1], not_5_out);
  and and_19 (and_19_out, OUTPUTS[1], not_4_out, not_6_out);
  and and_20 (and_20_out, OUTPUTS[1], OUTPUTS[0], shf);
  and and_21 (and_21_out, not_4_out, 1'b1);
  and and_22 (and_22_out, OUTPUTS[0], not_5_out);
  or or_1 (or_1_out, and_3_out, and_4_out, and_5_out, and_6_out, and_7_out, and_8_out, and_9_out);
  or or_2 (or_2_out, and_10_out, and_11_out, and_12_out, and_13_out, and_14_out, and_15_out);
  or or_3 (or_3_out, and_16_out, and_17_out, and_18_out, and_19_out, and_20_out);
  or or_4 (or_4_out, and_21_out, and_22_out);

  // Notes on the sheet:
  //   0x0F
  //   0xF0
endmodule

module INC_DEC_EIGHT_BIT_COUNTER (
  input  CLOCK,
  input  INC_DEC,
  output [7:0] NUM,
  output CARRY,
  output BORROW
);

  wire inc_dec_four_bit_counter_1_borrow, inc_dec_four_bit_counter_1_carry, or_1_out;

  INC_DEC_FOUR_BIT_COUNTER inc_dec_four_bit_counter_1 (
    .clk(CLOCK), .shf(INC_DEC), .BORROW(inc_dec_four_bit_counter_1_borrow),
    .CARRY(inc_dec_four_bit_counter_1_carry), .OUTPUTS(NUM[3:0]));
  or or_1 (or_1_out, inc_dec_four_bit_counter_1_carry, inc_dec_four_bit_counter_1_borrow);
  INC_DEC_FOUR_BIT_COUNTER inc_dec_four_bit_counter_2 (
    .clk(or_1_out), .shf(INC_DEC), .BORROW(BORROW), .CARRY(CARRY), .OUTPUTS(NUM[7:4]));
endmodule

module CONTROL_LOGIC_UNIT (
  input  RESET,
  input  Clock,
  input  [15:0] RAM_IN,
  input  [15:0] R1_IN,
  input  [15:0] R2_IN,
  input  [15:0] PROGRAM_COUNTER,
  output SAVE_REGISTER,
  output SAVE_TO_RAM,
  output HALT,
  output SAVE_VIDEO_VALUE,
  output SAVE_VIDEO_X_AXIS,
  output SAVE_VIDEO_Y_AXIS,
  output JUMP,
  output [15:0] RESULT,
  output [15:0] RAM_ADDRESS,
  output [15:0] RAM_OUT,
  output [3:0] REGISTER_1_ADDRESS,
  output [3:0] REGISTER_2_ADDRESS
);

  wire and_1_out, clu_helper_categoriser_1_compare, clu_helper_categoriser_1_cycle_2_out,
       clu_helper_categoriser_1_cycle_3_out, clu_helper_command_1_equal, clu_helper_command_1_greater,
       clu_helper_command_1_less, clu_helper_command_1_negative, clu_helper_command_1_overflow,
       clu_helper_command_1_zero, clu_helper_cycle_manager_1_final_cycle,
       clu_helper_cycle_manager_1_first_cycle, clu_helper_cycle_manager_1_out_8,
       clu_helper_cycle_manager_1_second_cycle, clu_helper_cycle_manager_1_third_cycle,
       clu_helper_register_manager_1_p9, clu_helper_register_manager_1_p10,
       clu_helper_register_manager_1_p11, clu_helper_register_manager_1_p12,
       clu_helper_register_manager_1_p13, clu_helper_register_manager_1_p14,
       clu_helper_register_manager_1_p15, ram_1_p1, ram_1_p5, undriven;
  wire [1:0] clu_helper_categoriser_1_carry;
  wire [7:0] clu_helper_register_manager_1_p16;
  wire [14:0] clu_helper_categoriser_1_jump_commands;
  wire [15:0] clu_helper_register_manager_1_p17, clu_helper_register_manager_1_p18, ram_1_p2;

  // RAM #(.addrWidth(16), .dataWidth(16), .enables("line"), .line("quad"), .\type ("nonvolatile")) ram_1: pin names not known; wires that end beside it: ram_1_p1, ram_1_p2, ram_1_p1, Clock, ram_1_p5
  SIXTEEN_BIT_PROGRAM_COUNTER sixteen_bit_program_counter_1 (
    .CLOCK(Clock), .RESET(RESET), .INP(RESULT), .WRITE(JUMP), .COUNT(ram_1_p2));
  CLU_Helper_Cycle_Manager clu_helper_cycle_manager_1 (
    .CLOCK(Clock), .CYCLE_2(clu_helper_categoriser_1_cycle_2_out), .RESET(RESET),
    .CYCLE_3(clu_helper_categoriser_1_cycle_3_out), .SECOND_CYCLE(clu_helper_cycle_manager_1_second_cycle),
    .FIRST_CYCLE(clu_helper_cycle_manager_1_first_cycle),
    .THIRD_CYCLE(clu_helper_cycle_manager_1_third_cycle), .out_8(clu_helper_cycle_manager_1_out_8),
    .FINAL_CYCLE(clu_helper_cycle_manager_1_final_cycle));  // open: out_10
  and and_1 (and_1_out, clu_helper_cycle_manager_1_out_8, ~clu_helper_cycle_manager_1_final_cycle);  // AND_Gate
  // CLU_Helper_Register_Manager clu_helper_register_manager_1: pin names not known; wires that end beside it: ram_1_p5, clu_helper_cycle_manager_1_first_cycle, clu_helper_cycle_manager_1_second_cycle, Clock, RESET, RAM_IN, R1_IN, R2_IN, clu_helper_register_manager_1_p9, clu_helper_register_manager_1_p10, clu_helper_register_manager_1_p11, clu_helper_register_manager_1_p12, clu_helper_register_manager_1_p13, clu_helper_register_manager_1_p14, clu_helper_register_manager_1_p15, clu_helper_register_manager_1_p16, clu_helper_register_manager_1_p17, clu_helper_register_manager_1_p18, RAM_ADDRESS, RAM_OUT, REGISTER_1_ADDRESS, REGISTER_2_ADDRESS
  CLU_Helper_Categoriser clu_helper_categoriser_1 (
    .CYCLE_1(clu_helper_cycle_manager_1_first_cycle), .CYCLE_2(clu_helper_cycle_manager_1_second_cycle),
    .CYCLE_3(clu_helper_cycle_manager_1_third_cycle), .INSTRUCTION(clu_helper_register_manager_1_p16),
    .JUMP_COMMANDS(clu_helper_categoriser_1_jump_commands), .HALT(HALT),
    .SAVE_VIDEO_Y_AXIS(SAVE_VIDEO_Y_AXIS), .SAVE_VIDEO_X_AXIS(SAVE_VIDEO_X_AXIS),
    .SAVE_VIDEO_VALUE(SAVE_VIDEO_VALUE), .CYCLE_2_OUT(clu_helper_categoriser_1_cycle_2_out),
    .CYCLE_3_OUT(clu_helper_categoriser_1_cycle_3_out), .DEST_REG(clu_helper_register_manager_1_p9),
    .SOURCE_REG(clu_helper_register_manager_1_p10), .SOURCE_IMM8(clu_helper_register_manager_1_p13),
    .SOURCE_RAM(clu_helper_register_manager_1_p12), .DEST_RAM(clu_helper_register_manager_1_p11),
    .SAVE_RAM(SAVE_TO_RAM), .SAVE_REG(SAVE_REGISTER), .CARRY(clu_helper_categoriser_1_carry),
    .CALL(clu_helper_register_manager_1_p14), .RTRN(clu_helper_register_manager_1_p15),
    .COMPARE(clu_helper_categoriser_1_compare));  // open: FINAL_CYCLE, NOP
  CLU_Helper_Command clu_helper_command_1 (
    .FINAL_CYCLE(undriven), .PROGRAM_COUNTER(PROGRAM_COUNTER), .WRITE_RAM(SAVE_TO_RAM),
    .WRITE_REG(SAVE_REGISTER), .INSTRUCTION(clu_helper_register_manager_1_p16),
    .COMPARE(clu_helper_categoriser_1_compare), .DESTINATION(clu_helper_register_manager_1_p17),
    .SOURCE(clu_helper_register_manager_1_p18), .RESET(RESET), .CARRY_IN(clu_helper_categoriser_1_carry),
    .OVERFLOW(clu_helper_command_1_overflow), .RESULT(RESULT), .GREATER(clu_helper_command_1_greater),
    .EQUAL(clu_helper_command_1_equal), .LESS(clu_helper_command_1_less),
    .NEGATIVE(clu_helper_command_1_negative), .ZERO(clu_helper_command_1_zero));
  CLU_Helper_Jump_Manager clu_helper_jump_manager_1 (
    .NEGATIVE(clu_helper_command_1_overflow), .CARRY(clu_helper_command_1_negative),
    .ZERO(clu_helper_command_1_zero), .LESS(clu_helper_command_1_less),
    .GREATER(clu_helper_command_1_greater), .EQUAL(clu_helper_command_1_equal), .FINAL_CYCLE(and_1_out),
    .JUMP_COMMANDS(clu_helper_categoriser_1_jump_commands), .JUMP(JUMP));
endmodule

module CLU_Helper_Command (
  input  [1:0] CARRY_IN,
  input  FINAL_CYCLE,
  input  RESET,
  input  COMPARE,
  input  [15:0] DESTINATION,
  input  [15:0] SOURCE,
  input  WRITE_RAM,
  input  WRITE_REG,
  input  [7:0] INSTRUCTION,
  input  [15:0] PROGRAM_COUNTER,
  output OVERFLOW,
  output GREATER,
  output EQUAL,
  output LESS,
  output NEGATIVE,
  output ZERO,
  output [15:0] RESULT
);

  wire adder_1_cout, multiplexer_1_out, or_2_out, subtractor_1_bout;
  wire [1:1] comparator_2_eq;
  wire [2:0] comparator_1_gt;
  wire [15:0] adder_1_out, and_1_out, divider_1_out, divider_1_rem, multiplexer_2_out, multiplexer_3_out,
       multiplexer_4_out, multiplexer_5_out, multiplier_1_out, negator_1_out, nor_1_out, not_1_out, or_1_out,
       shifter_1_out, shifter_2_out, shifter_3_out, shifter_4_out, shifter_5_out, subtractor_1_out;

  Adder #(.width(16)) adder_1 (.a(DESTINATION), .b(SOURCE), .out(adder_1_out), .cout(adder_1_cout));  // open: cin
  Subtractor #(.width(16)) subtractor_1 (
    .a(DESTINATION), .b(SOURCE), .out(subtractor_1_out), .bout(subtractor_1_bout));  // open: bin
  Multiplier #(.mode("twosComplement"), .width(16)) multiplier_1 (
    .a(DESTINATION), .b(SOURCE), .out(multiplier_1_out));  // open: cin, cout
  Divider #(.mode("twosComplement"), .width(16)) divider_1 (
    .a(DESTINATION), .b(SOURCE), .out(divider_1_out), .rem(divider_1_rem));  // open: upper
  assign and_1_out = DESTINATION & SOURCE;  // AND_Gate and_1, 16 bits wide
  assign or_1_out = DESTINATION | SOURCE;  // OR_Gate or_1, 16 bits wide
  assign nor_1_out = ~(DESTINATION | SOURCE);  // NOR_Gate nor_1, 16 bits wide
  Shifter #(.width(16)) shifter_1 (.in(DESTINATION), .\dist (SOURCE[3:0]), .out(shifter_1_out));
  Shifter #(.shift("lr"), .width(16)) shifter_2 (.in(DESTINATION), .\dist (SOURCE[3:0]), .out(shifter_2_out));
  Shifter #(.shift("rl"), .width(16)) shifter_3 (.in(DESTINATION), .\dist (SOURCE[3:0]), .out(shifter_3_out));
  Shifter #(.shift("rr"), .width(16)) shifter_4 (.in(DESTINATION), .\dist (SOURCE[3:0]), .out(shifter_4_out));
  Shifter #(.shift("ar"), .width(16)) shifter_5 (.in(DESTINATION), .\dist (SOURCE[3:0]), .out(shifter_5_out));
  Negator #(.width(16)) negator_1 (.in(SOURCE), .out(negator_1_out));
  assign not_1_out = ~SOURCE;  // NOT_Gate not_1, 16 bits wide
  Multiplexer multiplexer_1 (.in0(subtractor_1_bout), .in1(adder_1_cout), .out(multiplexer_1_out), .sel(CARRY_IN[1]));
  Register #(.width(1)) register_1 (
    .D(multiplexer_1_out), .en(CARRY_IN[0]), .clk(FINAL_CYCLE), .Q(OVERFLOW), .clr(RESET));
  Multiplexer #(.select(5), .width(16)) multiplexer_2 (
    .in0({16{1'b0}}), .in1({16{1'b0}}), .in2(SOURCE), .in3(SOURCE), .in4(SOURCE), .in5(SOURCE), .in6(SOURCE),
    .in7(SOURCE), .in8(SOURCE), .in9(SOURCE), .in10(SOURCE), .in11(SOURCE), .in12(SOURCE), .in13(SOURCE),
    .in14(SOURCE), .in15(SOURCE), .in16(SOURCE), .in17({16{1'b0}}), .in18({16{1'b0}}), .in19({16{1'b0}}),
    .in20({16{1'b0}}), .in21({16{1'b0}}), .in22({16{1'b0}}), .in23(adder_1_out), .in24(adder_1_out),
    .in25(adder_1_out), .in26(adder_1_out), .in27(adder_1_out), .in28(adder_1_out), .in29(subtractor_1_out),
    .in30(subtractor_1_out), .in31(subtractor_1_out), .out(multiplexer_2_out), .sel(INSTRUCTION[4:0]));
  Multiplexer #(.select(5), .width(16)) multiplexer_3 (
    .in0(subtractor_1_out), .in1(subtractor_1_out), .in2(subtractor_1_out), .in3(multiplier_1_out),
    .in4(multiplier_1_out), .in5(multiplier_1_out), .in6(multiplier_1_out), .in7(multiplier_1_out),
    .in8(multiplier_1_out), .in9(divider_1_out), .in10(divider_1_out), .in11(divider_1_out),
    .in12(divider_1_out), .in13(divider_1_out), .in14(divider_1_out), .in15(divider_1_rem),
    .in16(divider_1_rem), .in17(divider_1_rem), .in18(divider_1_rem), .in19(divider_1_rem),
    .in20(divider_1_rem), .in21(and_1_out), .in22(and_1_out), .in23(and_1_out), .in24(and_1_out),
    .in25(and_1_out), .in26(and_1_out), .in27(or_1_out), .in28(or_1_out), .in29(or_1_out), .in30(or_1_out),
    .in31(or_1_out), .out(multiplexer_3_out), .sel(INSTRUCTION[4:0]));
  Multiplexer #(.select(5), .width(16)) multiplexer_4 (
    .in0(or_1_out), .in1(nor_1_out), .in2(nor_1_out), .in3(nor_1_out), .in4(nor_1_out), .in5(nor_1_out),
    .in6(nor_1_out), .in7(shifter_1_out), .in8(shifter_1_out), .in9(shifter_1_out), .in10(shifter_1_out),
    .in11(shifter_1_out), .in12(shifter_1_out), .in13(shifter_2_out), .in14(shifter_2_out),
    .in15(shifter_2_out), .in16(shifter_2_out), .in17(shifter_2_out), .in18(shifter_2_out),
    .in19(shifter_3_out), .in20(shifter_3_out), .in21(shifter_3_out), .in22(shifter_3_out),
    .in23(shifter_3_out), .in24(shifter_3_out), .in25(shifter_4_out), .in26(shifter_4_out),
    .in27(shifter_4_out), .in28(shifter_4_out), .in29(shifter_4_out), .in30(shifter_4_out),
    .in31(shifter_5_out), .out(multiplexer_4_out), .sel(INSTRUCTION[4:0]));
  Multiplexer #(.select(5), .width(16)) multiplexer_5 (
    .in0(shifter_5_out), .in1(shifter_5_out), .in2(shifter_5_out), .in3(shifter_5_out), .in4(shifter_5_out),
    .in5(negator_1_out), .in6(negator_1_out), .in7(negator_1_out), .in8(negator_1_out), .in9(negator_1_out),
    .in10(negator_1_out), .in11(not_1_out), .in12(not_1_out), .in13(not_1_out), .in14(not_1_out),
    .in15(not_1_out), .in16(not_1_out), .in17(SOURCE), .in18(SOURCE), .in19(SOURCE), .in20(SOURCE),
    .in21(SOURCE), .in22(SOURCE), .in23(SOURCE), .in24(SOURCE), .in25(SOURCE), .in26(SOURCE), .in27(SOURCE),
    .in28(SOURCE), .in29(SOURCE), .in30(PROGRAM_COUNTER), .in31(SOURCE), .out(multiplexer_5_out),
    .sel(INSTRUCTION[4:0]));
  Comparator #(.width(16)) comparator_1 (
    .a(DESTINATION), .b(SOURCE), .gt(comparator_1_gt[0]), .eq(comparator_1_gt[1]), .lt(comparator_1_gt[2]));
  Multiplexer #(.select(2), .width(16)) multiplexer_6 (
    .in0(multiplexer_2_out), .in1(multiplexer_3_out), .in2(multiplexer_4_out), .in3(multiplexer_5_out),
    .out(RESULT), .sel(INSTRUCTION[6:5]));
  or or_2 (or_2_out, WRITE_RAM, WRITE_REG);
  Register #(.width(3)) register_2 (
    .D(comparator_1_gt), .en(COMPARE), .clk(FINAL_CYCLE), .Q({LESS, EQUAL, GREATER}), .clr(RESET));
  Comparator #(.width(16)) comparator_2 (.a({16{1'b0}}), .b(RESULT), .eq(comparator_2_eq[1]));  // open: gt, lt
  Register #(.width(2)) register_3 (
    .D({comparator_2_eq[1], RESULT[15]}), .en(or_2_out), .clk(FINAL_CYCLE), .Q({ZERO, NEGATIVE}), .clr(RESET));
endmodule

module CLU_Helper_Categoriser (
  input  FINAL_CYCLE,
  input  CYCLE_1,
  input  CYCLE_3,
  input  CYCLE_2,
  input  [7:0] INSTRUCTION,
  output SAVE_VIDEO_Y_AXIS,
  output SAVE_VIDEO_X_AXIS,
  output SAVE_VIDEO_VALUE,
  output NOP,
  output HALT,
  output COMPARE,
  output [1:0] CARRY,
  output CYCLE_3_OUT,
  output CYCLE_2_OUT,
  output SAVE_REG,
  output DEST_REG,
  output SOURCE_REG,
  output SOURCE_IMM8,
  output SOURCE_RAM,
  output DEST_RAM,
  output SAVE_RAM,
  output [14:0] JUMP_COMMANDS,
  output CALL,
  output RTRN
);

  wire and_7_out, and_8_out, and_10_out, and_11_out, demultiplexer_1_out0, demultiplexer_1_out1,
       demultiplexer_1_out2, demultiplexer_1_out3, demultiplexer_2_out2, demultiplexer_2_out3,
       demultiplexer_2_out4, demultiplexer_2_out5, demultiplexer_2_out6, demultiplexer_2_out7,
       demultiplexer_2_out8, demultiplexer_2_out9, demultiplexer_2_out10, demultiplexer_2_out11,
       demultiplexer_2_out12, demultiplexer_2_out13, demultiplexer_2_out14, demultiplexer_2_out15,
       demultiplexer_2_out16, demultiplexer_2_out17, demultiplexer_2_out18, demultiplexer_2_out19,
       demultiplexer_2_out20, demultiplexer_2_out21, demultiplexer_2_out22, demultiplexer_2_out23,
       demultiplexer_2_out24, demultiplexer_2_out25, demultiplexer_2_out26, demultiplexer_2_out27,
       demultiplexer_2_out28, demultiplexer_2_out29, demultiplexer_2_out30, demultiplexer_2_out31,
       demultiplexer_3_out0, demultiplexer_3_out1, demultiplexer_3_out2, demultiplexer_3_out3,
       demultiplexer_3_out4, demultiplexer_3_out5, demultiplexer_3_out6, demultiplexer_3_out7,
       demultiplexer_3_out8, demultiplexer_3_out9, demultiplexer_3_out10, demultiplexer_3_out11,
       demultiplexer_3_out12, demultiplexer_3_out13, demultiplexer_3_out14, demultiplexer_3_out15,
       demultiplexer_3_out16, demultiplexer_4_out0, demultiplexer_4_out1, demultiplexer_4_out2,
       demultiplexer_4_out3, demultiplexer_4_out4, demultiplexer_4_out5, demultiplexer_4_out6,
       demultiplexer_4_out7, demultiplexer_4_out8, demultiplexer_4_out9, demultiplexer_4_out10,
       demultiplexer_4_out11, demultiplexer_4_out12, demultiplexer_4_out13, demultiplexer_4_out14,
       demultiplexer_4_out15, demultiplexer_4_out16, demultiplexer_4_out17, demultiplexer_4_out18,
       demultiplexer_4_out19, demultiplexer_4_out20, demultiplexer_4_out21, demultiplexer_4_out22,
       demultiplexer_4_out23, demultiplexer_4_out24, demultiplexer_4_out25, demultiplexer_4_out26,
       demultiplexer_4_out27, demultiplexer_4_out28, demultiplexer_4_out29, demultiplexer_4_out30,
       demultiplexer_4_out31, demultiplexer_5_out0, demultiplexer_5_out1, demultiplexer_5_out2,
       demultiplexer_5_out3, demultiplexer_5_out4, demultiplexer_5_out5, demultiplexer_5_out6,
       demultiplexer_5_out7, demultiplexer_5_out8, demultiplexer_5_out9, demultiplexer_5_out10,
       demultiplexer_5_out11, demultiplexer_5_out12, demultiplexer_5_out13, demultiplexer_5_out14,
       demultiplexer_5_out15, demultiplexer_5_out16, demultiplexer_5_out17, demultiplexer_5_out18,
       demultiplexer_5_out19, demultiplexer_5_out20, demultiplexer_5_out21, demultiplexer_5_out22,
       demultiplexer_5_out23, demultiplexer_5_out24, demultiplexer_5_out25, demultiplexer_5_out26,
       demultiplexer_5_out27, demultiplexer_5_out28, demultiplexer_5_out29, demultiplexer_5_out30,
       demultiplexer_5_out31, IMM8_out, JUMP_out, or_3_out, or_4_out, or_5_out, or_6_out, or_7_out, or_8_out,
       or_9_out, or_10_out, or_11_out, or_12_out, or_13_out, or_14_out, or_15_out, or_16_out, or_17_out,
       or_18_out, or_19_out, or_20_out, or_21_out, or_22_out, or_23_out, or_24_out, or_25_out, or_26_out,
       or_27_out, or_28_out, or_29_out, or_30_out, or_31_out, or_32_out, or_34_out, or_35_out, or_36_out,
       or_37_out, or_38_out, or_41_out, or_42_out, RAM_IMM8_out, RAM_out, RAM_RAM_out, RAM_REG_out,
       REG_IMM8_out, REG_RAM_out, REG_REG_out, REGR_out, SUB_out;

  or or_1 (CARRY[0], CARRY[1], SUB_out);
  Demultiplexer #(.select(2)) demultiplexer_1 (
    .out0(demultiplexer_1_out0), .out1(demultiplexer_1_out1), .out2(demultiplexer_1_out2),
    .out3(demultiplexer_1_out3), .in(1'b1), .sel(INSTRUCTION[6:5]));
  Demultiplexer #(.select(5)) demultiplexer_2 (
    .out0(NOP), .out1(HALT), .out2(demultiplexer_2_out2), .out3(demultiplexer_2_out3),
    .out4(demultiplexer_2_out4), .out5(demultiplexer_2_out5), .out6(demultiplexer_2_out6),
    .out7(demultiplexer_2_out7), .out8(demultiplexer_2_out8), .out9(demultiplexer_2_out9),
    .out10(demultiplexer_2_out10), .out11(demultiplexer_2_out11), .out12(demultiplexer_2_out12),
    .out13(demultiplexer_2_out13), .out14(demultiplexer_2_out14), .out15(demultiplexer_2_out15),
    .out16(demultiplexer_2_out16), .out17(demultiplexer_2_out17), .out18(demultiplexer_2_out18),
    .out19(demultiplexer_2_out19), .out20(demultiplexer_2_out20), .out21(demultiplexer_2_out21),
    .out22(demultiplexer_2_out22), .out23(demultiplexer_2_out23), .out24(demultiplexer_2_out24),
    .out25(demultiplexer_2_out25), .out26(demultiplexer_2_out26), .out27(demultiplexer_2_out27),
    .out28(demultiplexer_2_out28), .out29(demultiplexer_2_out29), .out30(demultiplexer_2_out30),
    .out31(demultiplexer_2_out31), .in(demultiplexer_1_out0), .sel(INSTRUCTION[4:0]));
  or or_2 (COMPARE, demultiplexer_2_out17, demultiplexer_2_out18, demultiplexer_2_out19, demultiplexer_2_out20, demultiplexer_2_out21, demultiplexer_2_out22);
  or ADD (CARRY[1], demultiplexer_2_out23, demultiplexer_2_out24, demultiplexer_2_out25, demultiplexer_2_out26, demultiplexer_2_out27, demultiplexer_2_out28);
  Demultiplexer #(.select(5)) demultiplexer_3 (
    .out0(demultiplexer_3_out0), .out1(demultiplexer_3_out1), .out2(demultiplexer_3_out2),
    .out3(demultiplexer_3_out3), .out4(demultiplexer_3_out4), .out5(demultiplexer_3_out5),
    .out6(demultiplexer_3_out6), .out7(demultiplexer_3_out7), .out8(demultiplexer_3_out8),
    .out9(demultiplexer_3_out9), .out10(demultiplexer_3_out10), .out11(demultiplexer_3_out11),
    .out12(demultiplexer_3_out12), .out13(demultiplexer_3_out13), .out14(demultiplexer_3_out14),
    .out15(demultiplexer_3_out15), .out16(demultiplexer_3_out16), .out17(JUMP_COMMANDS[0]),
    .out18(JUMP_COMMANDS[1]), .out19(JUMP_COMMANDS[2]), .out20(JUMP_COMMANDS[3]), .out21(JUMP_COMMANDS[4]),
    .out22(JUMP_COMMANDS[5]), .out23(JUMP_COMMANDS[6]), .out24(JUMP_COMMANDS[7]), .out25(JUMP_COMMANDS[8]),
    .out26(JUMP_COMMANDS[9]), .out27(JUMP_COMMANDS[10]), .out28(JUMP_COMMANDS[11]),
    .out29(JUMP_COMMANDS[12]), .out30(CALL), .out31(JUMP_COMMANDS[14]), .in(demultiplexer_1_out3),
    .sel(INSTRUCTION[4:0]));
  or SUB (SUB_out, demultiplexer_2_out29, demultiplexer_2_out30, demultiplexer_2_out31, demultiplexer_4_out2, demultiplexer_4_out1, demultiplexer_4_out0);
  Demultiplexer #(.select(5)) demultiplexer_4 (
    .out0(demultiplexer_4_out0), .out1(demultiplexer_4_out1), .out2(demultiplexer_4_out2),
    .out3(demultiplexer_4_out3), .out4(demultiplexer_4_out4), .out5(demultiplexer_4_out5),
    .out6(demultiplexer_4_out6), .out7(demultiplexer_4_out7), .out8(demultiplexer_4_out8),
    .out9(demultiplexer_4_out9), .out10(demultiplexer_4_out10), .out11(demultiplexer_4_out11),
    .out12(demultiplexer_4_out12), .out13(demultiplexer_4_out13), .out14(demultiplexer_4_out14),
    .out15(demultiplexer_4_out15), .out16(demultiplexer_4_out16), .out17(demultiplexer_4_out17),
    .out18(demultiplexer_4_out18), .out19(demultiplexer_4_out19), .out20(demultiplexer_4_out20),
    .out21(demultiplexer_4_out21), .out22(demultiplexer_4_out22), .out23(demultiplexer_4_out23),
    .out24(demultiplexer_4_out24), .out25(demultiplexer_4_out25), .out26(demultiplexer_4_out26),
    .out27(demultiplexer_4_out27), .out28(demultiplexer_4_out28), .out29(demultiplexer_4_out29),
    .out30(demultiplexer_4_out30), .out31(demultiplexer_4_out31), .in(demultiplexer_1_out1),
    .sel(INSTRUCTION[4:0]));
  Demultiplexer #(.select(5)) demultiplexer_5 (
    .out0(demultiplexer_5_out0), .out1(demultiplexer_5_out1), .out2(demultiplexer_5_out2),
    .out3(demultiplexer_5_out3), .out4(demultiplexer_5_out4), .out5(demultiplexer_5_out5),
    .out6(demultiplexer_5_out6), .out7(demultiplexer_5_out7), .out8(demultiplexer_5_out8),
    .out9(demultiplexer_5_out9), .out10(demultiplexer_5_out10), .out11(demultiplexer_5_out11),
    .out12(demultiplexer_5_out12), .out13(demultiplexer_5_out13), .out14(demultiplexer_5_out14),
    .out15(demultiplexer_5_out15), .out16(demultiplexer_5_out16), .out17(demultiplexer_5_out17),
    .out18(demultiplexer_5_out18), .out19(demultiplexer_5_out19), .out20(demultiplexer_5_out20),
    .out21(demultiplexer_5_out21), .out22(demultiplexer_5_out22), .out23(demultiplexer_5_out23),
    .out24(demultiplexer_5_out24), .out25(demultiplexer_5_out25), .out26(demultiplexer_5_out26),
    .out27(demultiplexer_5_out27), .out28(demultiplexer_5_out28), .out29(demultiplexer_5_out29),
    .out30(demultiplexer_5_out30), .out31(demultiplexer_5_out31), .in(demultiplexer_1_out2),
    .sel(INSTRUCTION[4:0]));
  or JUMP (JUMP_out, JUMP_COMMANDS[0], JUMP_COMMANDS[1], JUMP_COMMANDS[2], JUMP_COMMANDS[3], JUMP_COMMANDS[4], JUMP_COMMANDS[5], JUMP_COMMANDS[6], JUMP_COMMANDS[8], JUMP_COMMANDS[9], JUMP_COMMANDS[10], JUMP_COMMANDS[11], JUMP_COMMANDS[12], CALL, JUMP_COMMANDS[7]);
  or or_3 (or_3_out, demultiplexer_2_out10, demultiplexer_2_out9, demultiplexer_2_out8);
  or or_4 (or_4_out, demultiplexer_2_out7, demultiplexer_2_out6, demultiplexer_2_out5);
  or or_5 (or_5_out, demultiplexer_2_out4, demultiplexer_2_out3, demultiplexer_2_out2);
  or REGR (REGR_out, demultiplexer_2_out2, demultiplexer_2_out5, demultiplexer_2_out8);
  or IMM8 (IMM8_out, demultiplexer_2_out3, demultiplexer_2_out6, demultiplexer_2_out9);
  or RAM (RAM_out, demultiplexer_2_out4, demultiplexer_2_out7, demultiplexer_2_out10);
  and and_1 (SAVE_VIDEO_Y_AXIS, FINAL_CYCLE, or_3_out);
  and and_2 (SAVE_VIDEO_X_AXIS, FINAL_CYCLE, or_4_out);
  and and_3 (SAVE_VIDEO_VALUE, FINAL_CYCLE, or_5_out);
  or or_6 (or_6_out, demultiplexer_2_out11, demultiplexer_2_out17, demultiplexer_2_out23, demultiplexer_2_out29);
  or or_7 (or_7_out, demultiplexer_2_out12, demultiplexer_2_out18, demultiplexer_2_out24, demultiplexer_2_out30);
  or or_8 (or_8_out, demultiplexer_2_out13, demultiplexer_2_out19, demultiplexer_2_out25, demultiplexer_2_out31);
  or or_9 (or_9_out, demultiplexer_2_out14, demultiplexer_2_out20, demultiplexer_2_out26, demultiplexer_4_out0);
  or or_10 (or_10_out, demultiplexer_2_out15, demultiplexer_2_out21, demultiplexer_2_out27, demultiplexer_4_out1);
  or or_11 (or_11_out, demultiplexer_2_out16, demultiplexer_2_out22, demultiplexer_2_out28, demultiplexer_4_out2);
  or or_12 (or_12_out, demultiplexer_4_out3, demultiplexer_4_out9, demultiplexer_4_out15, demultiplexer_4_out21, demultiplexer_4_out27);
  or or_13 (or_13_out, demultiplexer_4_out4, demultiplexer_4_out10, demultiplexer_4_out16, demultiplexer_4_out22, demultiplexer_4_out28);
  or or_14 (or_14_out, demultiplexer_4_out5, demultiplexer_4_out11, demultiplexer_4_out17, demultiplexer_4_out23, demultiplexer_4_out29);
  or or_15 (or_15_out, demultiplexer_4_out6, demultiplexer_4_out12, demultiplexer_4_out18, demultiplexer_4_out24, demultiplexer_4_out30);
  or or_16 (or_16_out, demultiplexer_4_out7, demultiplexer_4_out13, demultiplexer_4_out19, demultiplexer_4_out25, demultiplexer_4_out31);
  or or_17 (or_17_out, demultiplexer_4_out8, demultiplexer_4_out14, demultiplexer_4_out20, demultiplexer_4_out26, demultiplexer_5_out0);
  or or_18 (or_18_out, demultiplexer_5_out1, demultiplexer_5_out7, demultiplexer_5_out13, demultiplexer_5_out19, demultiplexer_5_out25);
  or or_19 (or_19_out, demultiplexer_5_out2, demultiplexer_5_out8, demultiplexer_5_out14, demultiplexer_5_out20, demultiplexer_5_out26);
  or or_20 (or_20_out, demultiplexer_5_out3, demultiplexer_5_out9, demultiplexer_5_out15, demultiplexer_5_out21, demultiplexer_5_out27);
  or or_21 (or_21_out, demultiplexer_5_out4, demultiplexer_5_out10, demultiplexer_5_out16, demultiplexer_5_out22, demultiplexer_5_out28);
  or or_22 (or_22_out, demultiplexer_5_out5, demultiplexer_5_out11, demultiplexer_5_out17, demultiplexer_5_out23, demultiplexer_5_out29);
  or or_23 (or_23_out, demultiplexer_5_out6, demultiplexer_5_out12, demultiplexer_5_out18, demultiplexer_5_out24, demultiplexer_5_out30);
  or or_24 (or_24_out, demultiplexer_5_out31, demultiplexer_3_out5, demultiplexer_3_out11);
  or or_25 (or_25_out, demultiplexer_3_out0, demultiplexer_3_out6, demultiplexer_3_out12);
  or or_26 (or_26_out, demultiplexer_3_out1, demultiplexer_3_out7, demultiplexer_3_out13);
  or or_27 (or_27_out, demultiplexer_3_out2, demultiplexer_3_out8, demultiplexer_3_out14);
  or or_28 (or_28_out, demultiplexer_3_out3, demultiplexer_3_out9, demultiplexer_3_out15);
  or or_29 (or_29_out, demultiplexer_3_out4, demultiplexer_3_out10, demultiplexer_3_out16);
  or or_30 (or_30_out, NOP, HALT, REGR_out);
  or REG_REG (REG_REG_out, or_6_out, or_12_out, or_18_out, or_24_out);
  or RAM_REG (RAM_REG_out, or_7_out, or_13_out, or_19_out, or_25_out);
  or REG_IMM8 (REG_IMM8_out, or_8_out, or_14_out, or_20_out, or_26_out);
  or REG_RAM (REG_RAM_out, or_9_out, or_15_out, or_21_out, or_27_out);
  or RAM_IMM8 (RAM_IMM8_out, or_10_out, or_16_out, or_22_out, or_28_out);
  or RAM_RAM (RAM_RAM_out, or_11_out, or_17_out, or_23_out, or_29_out);
  or or_31 (or_31_out, IMM8_out, RAM_out);
  or or_32 (or_32_out, or_30_out, JUMP_COMMANDS[14], REG_REG_out);
  and and_4 (CYCLE_3_OUT, ~or_32_out, ~CYCLE_2_OUT);  // AND_Gate
  or or_33 (CYCLE_2_OUT, or_31_out, RAM_REG_out, REG_IMM8_out, REG_RAM_out, JUMP_out);
  or or_34 (or_34_out, REG_REG_out, RAM_REG_out, REG_RAM_out);
  or or_35 (or_35_out, REG_REG_out, REGR_out, RAM_REG_out);
  or or_36 (or_36_out, IMM8_out, JUMP_out, REG_IMM8_out);
  or or_37 (or_37_out, RAM_out, REG_RAM_out);
  or or_38 (or_38_out, RAM_REG_out, RAM_IMM8_out, RAM_RAM_out);
  and and_5 (DEST_REG, CYCLE_1, or_34_out);
  and and_6 (SOURCE_REG, CYCLE_1, or_35_out);
  and and_7 (and_7_out, CYCLE_2, or_36_out);
  and and_8 (and_8_out, or_37_out, CYCLE_2);
  and and_9 (DEST_RAM, CYCLE_2, or_38_out);
  and and_10 (and_10_out, CYCLE_3, RAM_IMM8_out);
  and and_11 (and_11_out, CYCLE_3, RAM_RAM_out);
  or or_39 (SOURCE_IMM8, and_7_out, and_10_out);
  or or_40 (SOURCE_RAM, and_8_out, and_11_out);
  or or_41 (or_41_out, REG_REG_out, REG_IMM8_out, REG_RAM_out);
  or or_42 (or_42_out, RAM_REG_out, RAM_IMM8_out, RAM_RAM_out);
  and and_12 (SAVE_REG, COMPARE, FINAL_CYCLE, or_41_out);
  and and_13 (SAVE_RAM, ~COMPARE, FINAL_CYCLE, or_42_out);  // AND_Gate

  assign JUMP_COMMANDS[13] = CALL;
  assign RTRN = JUMP_COMMANDS[14];
endmodule

module CLU_Helper_Jump_Manager (
  input  NEGATIVE,
  input  CARRY,
  input  ZERO,
  input  LESS,
  input  GREATER,
  input  EQUAL,
  input  FINAL_CYCLE,
  input  [14:0] JUMP_COMMANDS,
  output JUMP
);

  wire JC_out, JEQ_out, JG_out, JGE_out, JL_out, JLE_out, JN_out, JNC_out, JNE_out, JNZ_out, JP_out, JZ_out,
       or_1_out, or_2_out, or_3_out;

  and JN (JN_out, JUMP_COMMANDS[11], NEGATIVE);
  and JP (JP_out, JUMP_COMMANDS[12], ~NEGATIVE);  // AND_Gate
  and JNC (JNC_out, JUMP_COMMANDS[9], ~CARRY);  // AND_Gate
  and JC (JC_out, JUMP_COMMANDS[10], CARRY);
  and JL (JL_out, JUMP_COMMANDS[5], LESS);
  and JNZ (JNZ_out, JUMP_COMMANDS[7], ~ZERO);  // AND_Gate
  and JZ (JZ_out, JUMP_COMMANDS[8], ZERO);
  and JG (JG_out, JUMP_COMMANDS[3], GREATER);
  or or_1 (or_1_out, EQUAL, LESS);
  or or_2 (or_2_out, EQUAL, GREATER);
  and JEQ (JEQ_out, JUMP_COMMANDS[1], EQUAL);
  and JNE (JNE_out, JUMP_COMMANDS[2], ~EQUAL);  // AND_Gate
  and JLE (JLE_out, or_1_out, JUMP_COMMANDS[4]);
  and JGE (JGE_out, or_2_out, JUMP_COMMANDS[6]);
  or or_3 (or_3_out, JUMP_COMMANDS[0], JEQ_out, JNE_out, JG_out, JLE_out, JL_out, JGE_out, JNZ_out, JZ_out, JNC_out, JC_out, JN_out, JP_out, JUMP_COMMANDS[13], JUMP_COMMANDS[14]);
  and and_1 (JUMP, FINAL_CYCLE, or_3_out);

  // Notes on the sheet:
  //   JUMP
  //   CALL
  //   RETURN
endmodule

module CLU_Helper_Cycle_Manager (
  input  CYCLE_2,
  input  CYCLE_3,
  input  CLOCK,
  input  RESET,
  output THIRD_CYCLE,
  output SECOND_CYCLE,
  output FIRST_CYCLE,
  output out_8,
  output FINAL_CYCLE,
  output out_10
);

  wire and_3_out, and_4_out, and_5_out, and_6_out, and_7_out, and_8_out, and_9_out, and_10_out, not_1_out,
       or_1_out, or_2_out, t_ff_1_q;

  and and_1 (SECOND_CYCLE, ~CLOCK, t_ff_1_q);  // AND_Gate
  T_Flip_Flop t_ff_1 (.T(CLOCK), .clk(CLOCK), .Q(t_ff_1_q), .reset(or_1_out));  // open: Qn, preset
  and and_2 (FIRST_CYCLE, CLOCK, and_3_out);
  and and_3 (and_3_out, ~t_ff_1_q, ~THIRD_CYCLE);  // AND_Gate
  T_Flip_Flop t_ff_2 (.T(t_ff_1_q), .clk(CLOCK), .Q(THIRD_CYCLE), .reset(or_1_out));  // open: Qn, preset
  or or_1 (or_1_out, or_2_out, RESET);
  and and_4 (and_4_out, ~CYCLE_2, ~CYCLE_3);  // AND_Gate
  and and_5 (and_5_out, CYCLE_2, THIRD_CYCLE);
  and and_6 (and_6_out, t_ff_1_q, THIRD_CYCLE);
  and and_7 (and_7_out, t_ff_1_q, and_4_out);
  or or_2 (or_2_out, and_7_out, and_5_out, and_6_out);
  and and_8 (and_8_out, and_4_out, and_3_out);
  and and_9 (and_9_out, CYCLE_2, SECOND_CYCLE);
  and and_10 (and_10_out, ~and_4_out, ~CYCLE_2, THIRD_CYCLE);  // AND_Gate
  or or_3 (out_8, and_8_out, and_9_out, and_10_out);
  D_Flip_Flop d_ff_1 (.D(out_8), .clk(CLOCK), .Q(FINAL_CYCLE), .reset(RESET));  // open: Qn, preset
  D_Flip_Flop d_ff_2 (.D(out_8), .clk(not_1_out), .Q(out_10), .reset(RESET));  // open: Qn, preset
  not not_1 (not_1_out, CLOCK);
endmodule

module CLU_Helper_Register_Manager (
  input  [15:0] REG_SOURCE_IN,
  input  SOURCE_IMM8,
  input  SOURCE_REG,
  input  [15:0] RAM_IN,
  input  SOURCE_RAM,
  input  [15:0] REG_DEST_IN,
  input  DEST_REG,
  input  DEST_RAM,
  input  RESET,
  input  FIRST_CYCLE,
  input  [15:0] INSTRUCTION_BUS,
  input  SECOND_CYCLE,
  input  RTRN,
  input  CALL,
  output [15:0] out_15,
  output [15:0] SOURCE_VALUE,
  output [1:0] out_17,
  output [15:0] DEST_VALUE,
  output [7:0] INSTRUCT,
  output [3:0] REG_SOURCE_OUT,
  output [15:0] RAM_DEST_INSTRUCT,
  output [3:0] REG_DEST_OUT,
  output [15:0] RAM_OUT
);

  wire or_1_out, or_2_out, or_3_out;
  wire [1:0] priority_encoder_2_out;
  wire [15:0] multiplexer_2_out, multiplexer_3_out;

  Priority_Encoder #(.select(2)) priority_encoder_1 (
    .in0(1'b1), .in1(1'b1), .in2(SOURCE_REG), .in3(SOURCE_RAM), .out(out_17));  // open: gs, en_out, en_in
  or or_1 (or_1_out, SOURCE_REG, SOURCE_IMM8, SOURCE_RAM);
  Priority_Encoder #(.select(2)) priority_encoder_2 (
    .in0(1'b1), .in1(1'b1), .in2(DEST_REG), .in3(DEST_RAM), .out(priority_encoder_2_out));  // open: gs, en_out, en_in
  or or_2 (or_2_out, DEST_REG, DEST_RAM);
  Multiplexer #(.select(2), .width(16)) multiplexer_1 (
    .in0(INSTRUCTION_BUS), .in1(INSTRUCTION_BUS), .in2(REG_SOURCE_IN), .in3(RAM_IN), .out(out_15),
    .sel(out_17));
  Multiplexer #(.select(2), .width(16)) multiplexer_2 (
    .in0(INSTRUCTION_BUS), .in1(INSTRUCTION_BUS), .in2(REG_DEST_IN), .in3(RAM_IN), .out(multiplexer_2_out),
    .sel(priority_encoder_2_out));
  Register #(.width(16)) register_1 (.D(INSTRUCTION_BUS), .Q(RAM_DEST_INSTRUCT), .clr(RESET));  // open: en, clk
  or or_3 (or_3_out, RTRN, CALL);
  Multiplexer #(.width(16)) multiplexer_3 (.in0(INSTRUCTION_BUS), .in1(16'h2), .out(multiplexer_3_out), .sel(or_3_out));
  Register #(.width(16)) register_2 (.D(out_15), .en(or_1_out), .clk(or_1_out), .Q(SOURCE_VALUE), .clr(RESET));
  Register #(.width(16)) register_3 (.D(multiplexer_2_out), .en(or_2_out), .clk(or_2_out), .Q(DEST_VALUE), .clr(RESET));
  Register INSTRUCTION (.D(INSTRUCTION_BUS[15:8]), .en(FIRST_CYCLE), .clk(FIRST_CYCLE), .Q(INSTRUCT), .clr(RESET));
  Register #(.width(4)) REG_SOURCE_INSTRUCT (
    .D(INSTRUCTION_BUS[7:4]), .en(FIRST_CYCLE), .clk(FIRST_CYCLE), .Q(REG_SOURCE_OUT), .clr(RESET));
  Register #(.width(4)) REG_DEST_INSTRUCT (
    .D(INSTRUCTION_BUS[3:0]), .en(FIRST_CYCLE), .clk(FIRST_CYCLE), .Q(REG_DEST_OUT), .clr(RESET));
  Register #(.width(16)) register_4 (
    .D(multiplexer_3_out), .en(SECOND_CYCLE), .clk(SECOND_CYCLE), .Q(RAM_OUT), .clr(RESET));
endmodule
